// Logisim project 4-1MUX.circ as structural Verilog: 3 circuits, main circuit main
module main (
  input  D0,
  input  D1,
  input  D2,
  input  D3,
  input  S0,
  input  S1,
  output Y
);

  wire _2_1MUX_2_y, _2_1MUX_y;

  _2_1MUX _2_1MUX (.D0(D0), .D1(D1), .S(S0), .Y(_2_1MUX_y));
  _2_1MUX _2_1MUX_2 (.D0(D2), .D1(D3), .S(S0), .Y(_2_1MUX_2_y));
  _2_1MUX _2_1MUX_3 (.D0(_2_1MUX_y), .D1(_2_1MUX_2_y), .S(S1), .Y(Y));
endmodule

module _2_1MUX (
  input  D0,
  input  D1,
  input  S,
  output Y
);

  wire and_1_out, and_2_out, not_1_out;

  not not_1 (not_1_out, S);
  and and_1 (and_1_out, D1, S);
  and and_2 (and_2_out, D0, not_1_out);
  or or_1 (Y, and_1_out, and_2_out);
endmodule

module _4_4_1MUX (
  input  in_1,
  input  in_2,
  input  in_3,
  input  in_4,
  input  in_5,
  input  in_6,
  input  in_7,
  input  in_8,
  input  S1,
  input  S2,
  input  in_11,
  input  in_12,
  input  in_13,
  input  in_14,
  input  in_15,
  input  in_16,
  input  in_17,
  input  in_18,
  output out_19,
  output out_20,
  output out_21,
  output out_22
);

  main main_1 (.D0(in_1), .D1(in_2), .D2(in_3), .D3(in_4), .S0(S1), .S1(S2), .Y(out_19));
  main main_2 (.D0(in_5), .D1(in_6), .D2(in_7), .D3(in_8), .S0(S1), .S1(S2), .Y(out_20));
  main main_3 (.D0(in_11), .D1(in_12), .D2(in_13), .D3(in_14), .S0(S1), .S1(S2), .Y(out_21));
  main main_4 (.D0(in_15), .D1(in_16), .D2(in_17), .D3(in_18), .S0(S1), .S1(S2), .Y(out_22));
endmodule
