// Logisim project 8-MUX.circ as structural Verilog
module _2_MUX (
  input  in_1,
  input  in_2,
  input  in_3,
  output out_4
);

  wire and_1_out, and_2_out, not_1_out;

  not not_1 (not_1_out, in_3);
  and and_1 (and_1_out, in_1, in_3);
  and and_2 (and_2_out, in_2, not_1_out);
  or or_1 (out_4, and_1_out, and_2_out);
endmodule

module _8_MUX (
  input  in_1,
  input  in_2,
  input  in_3,
  input  in_4,
  input  in_5,
  input  in_6,
  input  in_7,
  input  in_8,
  input  in_9,
  input  in_10,
  input  in_11
);

  _2_MUX u_2_mux_1 (.in_1(in_1), .in_2(in_2), .in_3(in_9));  // open: out_4
  _2_MUX u_2_mux_2 (.in_3(in_9));  // open: in_1, in_2, out_4
  _2_MUX u_2_mux_3 (.in_3(in_9));  // open: in_1, in_2, out_4
  _2_MUX u_2_mux_4 (.in_3(in_9));  // open: in_1, in_2, out_4
  _2_MUX u_2_mux_5 ();  // open: in_1, in_2, in_3, out_4
  _2_MUX u_2_mux_6 ();  // open: in_1, in_2, in_3, out_4
  _2_MUX u_2_mux_7 ();  // open: in_1, in_2, in_3, out_4
endmodule
