// Logisim project 优先权编码.circ as structural Verilog: 1 circuit, main circuit main
module main (
  input  a,
  input  b,
  input  c,
  input  d,
  input  e,
  input  f,
  input  g,
  input  h,
  output w,
  output y,
  output t,
  output z
);

  wire nand_1_out, nand_2_out, nand_3_out, nand_4_out, nand_5_out, nand_6_out, nand_7_out, nand_8_out,
       nand_9_out, nand_10_out, nand_11_out, nand_12_out, nand_13_out, nand_14_out, nand_15_out, nand_16_out,
       nand_17_out, nand_18_out, nand_19_out, nand_20_out, nand_24_out;

  nand nand_1 (nand_1_out, h, h);
  nand nand_2 (nand_2_out, g, g);
  nand nand_3 (nand_3_out, f, f);
  nand nand_4 (nand_4_out, e, e);
  nand nand_5 (nand_5_out, h, h);
  nand nand_6 (nand_6_out, g, g);
  nand nand_7 (nand_7_out, d, d);
  nand nand_8 (nand_8_out, c, c);
  nand nand_9 (nand_9_out, h, h);
  nand nand_10 (nand_10_out, f, f);
  nand nand_11 (nand_11_out, d, d);
  nand nand_12 (nand_12_out, b, b);
  nand nand_13 (nand_13_out, a, a);
  nand nand_14 (nand_14_out, a, a);
  nand nand_15 (nand_15_out, b, b);
  nand nand_16 (nand_16_out, c, c);
  nand nand_17 (nand_17_out, d, d);
  nand nand_18 (nand_18_out, e, e);
  nand nand_19 (nand_19_out, g, g);
  nand nand_20 (nand_20_out, h, h);
  nand nand_21 (w, nand_1_out, nand_2_out, nand_3_out, nand_4_out);
  nand nand_22 (y, nand_5_out, nand_6_out, nand_7_out, nand_8_out);
  nand nand_23 (t, nand_9_out, nand_10_out, nand_11_out, nand_12_out, nand_13_out);
  nand nand_24 (nand_24_out, nand_14_out, nand_15_out, nand_16_out, nand_17_out, nand_18_out, nand_19_out, nand_20_out);
  nand nand_25 (z, nand_24_out, nand_24_out);
endmodule
