// Logisim project 奇校验器.circ as structural Verilog: 1 circuit, main circuit main
module main (
  input  X,
  input  Y,
  input  Z,
  input  W,
  output F
);

  wire and_1_out, and_2_out, and_3_out, and_4_out, and_5_out, and_6_out, and_7_out, and_8_out, not_1_out,
       not_2_out, not_3_out, not_4_out, not_5_out, not_6_out, not_7_out, not_8_out, not_9_out, not_10_out,
       not_11_out, not_12_out, not_13_out, not_14_out, not_15_out, not_16_out;

  not not_1 (not_1_out, X);
  not not_2 (not_2_out, Y);
  not not_3 (not_3_out, Z);
  not not_4 (not_4_out, X);
  not not_5 (not_5_out, Y);
  not not_6 (not_6_out, W);
  not not_7 (not_7_out, X);
  not not_8 (not_8_out, Z);
  not not_9 (not_9_out, W);
  not not_10 (not_10_out, X);
  not not_11 (not_11_out, Y);
  not not_12 (not_12_out, Z);
  not not_13 (not_13_out, W);
  not not_14 (not_14_out, Y);
  not not_15 (not_15_out, Z);
  not not_16 (not_16_out, W);
  and and_1 (and_1_out, not_1_out, not_2_out, not_3_out, W);
  and and_2 (and_2_out, not_4_out, not_5_out, Z, not_6_out);
  and and_3 (and_3_out, not_7_out, Y, not_8_out, not_9_out);
  and and_4 (and_4_out, not_10_out, Y, Z, W);
  and and_5 (and_5_out, X, not_11_out, not_12_out, not_13_out);
  and and_6 (and_6_out, X, not_14_out, Z, W);
  and and_7 (and_7_out, X, Y, not_15_out, W);
  and and_8 (and_8_out, X, Y, Z, not_16_out);
  or or_1 (F, and_1_out, and_2_out, and_3_out, and_4_out, and_5_out, and_6_out, and_7_out, and_8_out);
endmodule
