// Logisim project 实现多数表决器.circ as structural Verilog: 1 circuit, main circuit main
module main (
  input  X,
  input  Y,
  input  Z,
  output OUTPUT
);

  wire X_Y_out, X_Z_out, Y_Z_out;

  and X_Y (X_Y_out, X, Y);
  and Y_Z (Y_Z_out, Y, Z);
  and X_Z (X_Z_out, X, Z);
  or or_1 (OUTPUT, X_Y_out, Y_Z_out, X_Z_out);
endmodule
