// Logisim project lab2.3.circ as structural Verilog: 2 circuits, main circuit main
module main (
  input  [3:0] X,
  input  [3:0] Y,
  input  Cin,
  output [3:0] F,
  output Cout
);

  wire adder_1_cout, subtractor_1_bout;
  wire [3:0] adder_1_out, subtractor_1_out;

  Hex_Digit_Display hex_digit_display_1 ();  // open: value, dp
  Adder #(.width(4)) adder_1 (.a(X), .b(Y), .out(adder_1_out), .cout(adder_1_cout));  // open: cin
  Subtractor #(.width(4)) subtractor_1 (.a(X), .b(Y), .out(subtractor_1_out), .bout(subtractor_1_bout));  // open: bin
  Hex_Digit_Display hex_digit_display_2 ();  // open: value, dp
  FA FA0 ();  // open: A, B, Cin, Cout, F
  Hex_Digit_Display hex_digit_display_3 ();  // open: value, dp
  FA FA1 ();  // open: A, B, Cin, Cout, F
  Multiplexer #(.enable("false")) multiplexer_1 (.in0(adder_1_cout), .in1(subtractor_1_bout), .out(Cout), .sel(Cin));
  FA FA2 ();  // open: A, B, Cin, Cout, F
  Multiplexer #(.width(4), .enable("false")) multiplexer_2 (
    .in0(adder_1_out), .in1(subtractor_1_out), .out(F), .sel(Cin));
  FA FA3 ();  // open: A, B, Cin, Cout, F

  // Other names for the same wires on the sheet: SUM[3:0] = F; 操作数x[3:0] = X; 操作数y[3:0] = Y

  // Notes on the sheet:
  //   输入引脚
  //   +
  //   =
  //   请勿修改引脚名称、电路名称及电路封装外观
  //   提示：使用独立逻辑门及全加器FA子电路实现4位二进制数加减法器，禁止直接使用加减法器组件。
  //   输出引脚
endmodule

module FA (
  input  A,
  input  B,
  input  Cin,
  output F,
  output Cout
);


  // Notes on the sheet:
  //   全加器
endmodule
