// Logisim project 闹钟.circ as structural Verilog: 9 circuits, main circuit main
module _61 (
  input  _0_Enable,
  input  LD,
  input  [3:0] Cin,
  input  Clk,
  output [3:0] Result,
  output Cout
);

  Counter #(.width(4), .max('h5)) counter_1 (
    .load(LD), .D(Cin), .count(_0_Enable), .Q(Result), .carry(Cout), .clk(Clk));  // open: clr, preset, down
endmodule

module main (
  input  CLK,
  input  LD,
  input  [3:0] HH1,
  input  [3:0] HH0,
  input  [3:0] MM1,
  input  [3:0] MM0,
  input  [3:0] SS1,
  input  [3:0] SS0,
  output [3:0] HH_H,
  output [3:0] HH_L,
  output [3:0] MM_H,
  output [3:0] MM_L,
  output [3:0] SS_H,
  output [3:0] SS_L,
  output LED_R,
  output LED_G,
  output LED_B,
  output INErr
);

  wire and_1_out, and_2_out, and_3_out, and_4_out, and_5_out, comparator_1_eq, comparator_1_gt,
       comparator_2_gt, comparator_3_gt, comparator_4_gt, comparator_5_gt, comparator_6_gt, LED_EN,
       n601_1_cout, n601_2_cout, or_1_out, or_2_out, or_3_out, or_4_out, START, STOP;
  wire [3:0] mod8_1_u;
  wire [3:3] gray_1_out_2;
  wire [4:0] counter_1_q;

  and and_1 (and_1_out, LD, ~INErr);  // AND_Gate
  Comparator #(.width(4), .mode("unsigned")) comparator_1 (
    .a(HH1), .b(4'b0010), .gt(comparator_1_gt), .eq(comparator_1_eq));  // open: lt
  Comparator #(.width(4), .mode("unsigned")) comparator_2 (.a(HH0), .b(4'b0011), .gt(comparator_2_gt));  // open: eq, lt
  Comparator #(.width(4), .mode("unsigned")) comparator_3 (.a(MM1), .b(4'b0101), .gt(comparator_3_gt));  // open: eq, lt
  Comparator #(.width(4), .mode("unsigned")) comparator_4 (.a(MM0), .b(4'b1001), .gt(comparator_4_gt));  // open: eq, lt
  Counter #(.width(5), .max('h13)) counter_1 (
    .D({5{1'b0}}), .count(LED_EN), .Q(counter_1_q), .carry(STOP), .clk(CLK), .clr(STOP));  // open: load, preset, down
  _241 u_241_1 (
    .LD(and_1_out), .Clk(CLK), .L(HH0), .H(HH1), .Enable(and_2_out), .L_out(HH_L), .H_out(HH_H));  // open: Cout
  _601 u_601_1 (
    .LD(and_1_out), .DH(MM1), .Clk(CLK), .DL(MM0), .Enable(n601_2_cout), .H_out(MM_H), .L_out(MM_L),
    .Cout(n601_1_cout));
  _601 u_601_2 (
    .LD(and_1_out), .DH(SS1), .Clk(CLK), .DL(SS0), .Enable(1'b1), .H_out(SS_H), .L_out(SS_L),
    .Cout(n601_2_cout));
  Comparator #(.width(4), .mode("unsigned")) comparator_5 (.a(SS1), .b(4'b0101), .gt(comparator_5_gt));  // open: eq, lt
  Comparator #(.width(4), .mode("unsigned")) comparator_6 (.a(SS0), .b(4'b1001), .gt(comparator_6_gt));  // open: eq, lt
  Hex_Digit_Display hex_digit_display_1 (.value(HH_H));  // open: dp
  and and_2 (and_2_out, n601_1_cout, n601_2_cout);
  and and_3 (and_3_out, comparator_1_eq, comparator_2_gt);
  and and_4 (and_4_out, comparator_3_gt, comparator_4_gt);
  and and_5 (and_5_out, comparator_5_gt, comparator_6_gt);
  Mod8 mod8_1 (
    .a(counter_1_q[3]), .b(counter_1_q[2]), .c(counter_1_q[1]), .d(counter_1_q[0]), .x(mod8_1_u[3]),
    .y(mod8_1_u[2]), .z(mod8_1_u[1]), .u(mod8_1_u[0]));
  Hex_Digit_Display hex_digit_display_2 (.value(MM_H));  // open: dp
  Hex_Digit_Display hex_digit_display_3 (.value(HH_L), .dp(1'b1));
  or or_1 (or_1_out, comparator_1_gt, and_3_out);
  or or_2 (or_2_out, comparator_3_gt, and_4_out, comparator_4_gt);
  or or_3 (or_3_out, comparator_5_gt, and_5_out, comparator_6_gt);
  Gray gray_1 (.in_1(mod8_1_u), .out_2({gray_1_out_2[3], LED_B, LED_G, LED_R}));
  and and_6 (START, LD, ~INErr);  // AND_Gate
  Hex_Digit_Display hex_digit_display_4 (.value(MM_L), .dp(1'b1));
  Hex_Digit_Display hex_digit_display_5 (.value(SS_H));  // open: dp
  Comparator #(.width(4), .mode("unsigned")) comparator_7 (.a(MM_H), .b(4'b0000));  // open: gt, eq, lt
  Hex_Digit_Display hex_digit_display_6 (.value(SS_L), .dp(1'b1));
  Register #(.width(1), .Select("low")) register_1 (
    .D(and_2_out), .Q(LED_EN), .clk(and_2_out), .clr(STOP));  // open: en
  or or_4 (or_4_out, or_1_out, or_2_out, or_3_out);
  and and_7 (INErr, or_4_out, LD);
  // RGBLed RGBLED: pin names not known; wires that end beside it: LED_R, LED_G, LED_B

  // Other names for the same wires on the sheet: H0[3:0] = HH_L; H1[3:0] = HH_H; M0[3:0] = MM_L; M1[3:0] = MM_H;
  //   S0[3:0] = SS_L; S1[3:0] = SS_H

  // Notes on the sheet:
  //   设置初始时间BCD码
  //   输入信号
  //   请勿修改引脚名称、电路名称及电路封装外观
  //   数字时钟
  //   提示：使用4位二进制加法计数器子电路、比较器和独立逻辑门组件实现数字时钟。
  //   在载入有效时，检测设置数据错误
  //   生成三色LED显示信号，持续10个时钟周期
endmodule

module _91 (
  input  _0_Enable,
  input  LD,
  input  [3:0] Cin,
  input  Reset,
  input  Clk,
  output [3:0] Result,
  output Cout
);

  Counter #(.width(4), .max('h9)) counter_1 (
    .load(LD), .D(Cin), .count(_0_Enable), .Q(Result), .carry(Cout), .clk(Clk), .clr(Reset));  // open: preset, down
endmodule

module _601 (
  input  LD,
  input  [3:0] DH,
  input  Clk,
  input  [3:0] DL,
  input  Enable,
  output [3:0] H_out,
  output [3:0] L_out,
  output Cout
);

  wire _6_cout, _10_cout, and_1_out, or_1_out, or_2_out;

  and and_1 (and_1_out, _10_cout, Enable);
  or or_1 (or_1_out, LD, and_1_out);
  Hex_Digit_Display hex_digit_display_1 (.value(H_out));  // open: dp
  _61 _6 (.LD(LD), .Cin(DH), .Clk(Clk), .Result(H_out), .Cout(_6_cout), ._0_Enable(or_1_out));
  or or_2 (or_2_out, LD, Enable);
  _91 _10 (.LD(LD), .Cin(DL), .Clk(Clk), .Result(L_out), .Cout(_10_cout), ._0_Enable(or_2_out));  // open: Reset
  Hex_Digit_Display hex_digit_display_2 (.value(L_out));  // open: dp
  and and_2 (Cout, _10_cout, _6_cout);
endmodule

module _241 (
  input  LD,
  input  Clk,
  input  [3:0] L,
  input  [3:0] H,
  input  Enable,
  output [3:0] L_out,
  output [3:0] H_out,
  output Cout
);

  wire and_1_out, and_2_out, n91_1_cout, or_1_out, or_2_out;

  or or_1 (or_1_out, LD, Enable);
  _91 u_91_1 (.LD(LD), .Cin(L), .Clk(Clk), .Result(L_out), .Cout(n91_1_cout), ._0_Enable(or_1_out), .Reset(and_2_out));
  or or_2 (or_2_out, LD, and_1_out);
  and and_1 (and_1_out, n91_1_cout, Enable);
  _91 u_91_2 (.LD(LD), .Cin(H), .Clk(Clk), .Result(H_out), ._0_Enable(or_2_out), .Reset(and_2_out));  // open: Cout
  and and_2 (and_2_out, H_out[1], L_out[2]);
  and and_3 (Cout, L_out[0], L_out[1], H_out[1]);
  Hex_Digit_Display hex_digit_display_1 (.value(H_out));  // open: dp
  Hex_Digit_Display hex_digit_display_2 (.value(L_out));  // open: dp
endmodule

module Gray (
  input  [3:0] in_1,
  output [3:0] out_2
);

  xor xor_1 (out_2[0], in_1[0], in_1[1]);
  xor xor_2 (out_2[1], in_1[1], in_1[2]);
  xor xor_3 (out_2[2], in_1[2], in_1[3]);

  assign out_2[3] = in_1[3];
endmodule

module Mod8 (
  input  a,
  input  b,
  input  c,
  input  d,
  output x,
  output y,
  output z,
  output u
);


  assign u = d;
  assign x = 1'b0;
  assign y = b;
  assign z = c;
endmodule

module _2 (
  input  in_1,
  input  in_2,
  output out_3
);

  Register #(.width(1), .Select("low")) register_1 (.D(in_1), .Q(out_3), .clk(in_2));  // open: en, clr
endmodule

module \闹钟  (
  input  CLK,
  input  [3:0] HH,
  input  [3:0] HL,
  input  [3:0] MH,
  input  [3:0] ML,
  input  [3:0] SH,
  input  [3:0] SL
);

  wire and_1_out, comparator_1_eq, comparator_2_eq, comparator_3_eq, comparator_4_eq, comparator_5_eq,
       comparator_6_eq;
  wire [3:0] main_1_hh_h, main_1_hh_l, main_1_mm_h, main_1_mm_l, main_1_ss_h, main_1_ss_l;

  main main_1 (
    .HH_H(main_1_hh_h), .HH_L(main_1_hh_l), .MM_H(main_1_mm_h), .MM_L(main_1_mm_l), .SS_H(main_1_ss_h),
    .SS_L(main_1_ss_l), .CLK(CLK));  // open: LD, HH1, HH0, MM1, MM0, SS1, SS0, INErr, LED_R, LED_G, LED_B
  Comparator #(.width(4)) comparator_1 (.a(main_1_hh_h), .b(HH), .eq(comparator_1_eq));  // open: gt, lt
  Comparator #(.width(4)) comparator_2 (.a(main_1_hh_l), .b(HL), .eq(comparator_2_eq));  // open: gt, lt
  Comparator #(.width(4)) comparator_3 (.a(main_1_mm_h), .b(MH), .eq(comparator_3_eq));  // open: gt, lt
  Comparator #(.width(4)) comparator_4 (.a(main_1_mm_l), .b(ML), .eq(comparator_4_eq));  // open: gt, lt
  Comparator #(.width(4)) comparator_5 (.a(main_1_ss_h), .b(SH), .eq(comparator_5_eq));  // open: gt, lt
  Comparator #(.width(4)) comparator_6 (.a(main_1_ss_l), .b(SL), .eq(comparator_6_eq));  // open: gt, lt
  and and_1 (and_1_out, comparator_1_eq, comparator_2_eq, comparator_3_eq, comparator_4_eq, comparator_5_eq, comparator_6_eq);
  // Buzzer buzzer_1: pin names not known; wires that end beside it: and_1_out
endmodule
