// Logisim project 随机数.circ as structural Verilog: 1 circuit, main circuit main
module main (
  input  Clk,
  output [7:0] out_2
);

  wire nand_1_out, xnor_1_out, xor_1_out, xor_2_out;

  nand nand_1 (nand_1_out, out_2[7], out_2[0]);
  xnor xnor_1 (xnor_1_out, out_2[6], out_2[1]);
  xor xor_1 (xor_1_out, out_2[5], out_2[2]);
  xor xor_2 (xor_2_out, out_2[3], out_2[4]);
  SHRG4U shrg4u_1 (
    .CLK(Clk), .CLR_L(1'b1), .Q3(out_2[7]), .Q2(out_2[6]), .D3(nand_1_out), .D2(xor_1_out), .D1(xor_2_out),
    .Q1(out_2[5]), .Q0(out_2[4]), .D0(xnor_1_out), .S1(1'b1), .S0(xnor_1_out));  // open: RIN, LIN
  SHRG4U shrg4u_2 (
    .CLK(Clk), .CLR_L(1'b1), .Q3(out_2[3]), .Q2(out_2[2]), .D3(out_2[7]), .D2(out_2[6]), .D1(out_2[5]),
    .Q1(out_2[1]), .Q0(out_2[0]), .D0(out_2[4]), .S1(1'b1), .S0(xor_2_out));  // open: RIN, LIN
endmodule
