// Logisim project lab4.4.circ as structural Verilog: 1 circuit, main circuit main
// 移位器
module main (
  input  [4:0] shamt,
  input  L_R,
  input  A_L,
  input  [31:0] DataIn,
  output [31:0] DataOut
);

  wire [0:0] multiplexer_2_out;
  wire [1:0] multiplexer_5_out;
  wire [1:1] multiplexer_4_out;
  wire [3:0] multiplexer_6_out, multiplexer_8_out;
  wire [3:3] multiplexer_7_out;
  wire [7:0] multiplexer_11_out;
  wire [7:7] multiplexer_10_out, multiplexer_13_out;
  wire [15:0] multiplexer_14_out;
  wire [27:0] multiplexer_6_out_2;
  wire [31:0] multiplexer_3_out, multiplexer_9_out, multiplexer_12_out;
  wire [31:31] multiplexer_1_out;

  Multiplexer #(.enable("false")) multiplexer_1 (.in0(1'b0), .in1(DataIn[31]), .out(multiplexer_1_out[31]), .sel(A_L));
  Multiplexer #(.enable("false")) multiplexer_2 (.in0(1'b0), .in1(DataIn[31]), .out(multiplexer_2_out[0]), .sel(A_L));
  Multiplexer #(.select(2), .width(32), .enable("false")) multiplexer_3 (
    .in0(DataIn), .in1(DataIn), .in2({multiplexer_1_out[31], DataIn[31:1]}),
    .in3({DataIn[30:0], multiplexer_2_out[0]}), .out(multiplexer_3_out), .sel({shamt[0], L_R}));
  Multiplexer #(.enable("false")) multiplexer_4 (
    .in0(1'b0), .in1(multiplexer_3_out[31]), .out(multiplexer_4_out[1]), .sel(A_L));
  Multiplexer #(.width(2), .enable("false")) multiplexer_5 (
    .in0(2'b00), .in1(multiplexer_3_out[31:30]), .out(multiplexer_5_out), .sel(A_L));
  Multiplexer #(.select(2), .width(32), .enable("false")) multiplexer_6 (
    .in0(multiplexer_3_out), .in1(multiplexer_3_out),
    .in2({{2{multiplexer_4_out[1]}}, multiplexer_3_out[31:2]}),
    .in3({multiplexer_3_out[29:0], multiplexer_5_out}), .out({multiplexer_6_out, multiplexer_6_out_2}),
    .sel({shamt[1], L_R}));
  Multiplexer #(.enable("false")) multiplexer_7 (
    .in0(1'b0), .in1(multiplexer_6_out[3]), .out(multiplexer_7_out[3]), .sel(A_L));
  Multiplexer #(.width(4), .enable("false")) multiplexer_8 (
    .in0(4'b0000), .in1(multiplexer_6_out), .out(multiplexer_8_out), .sel(A_L));
  Multiplexer #(.select(2), .width(32), .enable("false")) multiplexer_9 (
    .in0({multiplexer_6_out, multiplexer_6_out_2}), .in1({multiplexer_6_out, multiplexer_6_out_2}),
    .in2({{4{multiplexer_7_out[3]}}, multiplexer_6_out, multiplexer_6_out_2[27:4]}),
    .in3({multiplexer_6_out_2, multiplexer_8_out}), .out(multiplexer_9_out), .sel({shamt[2], L_R}));
  Multiplexer #(.enable("false")) multiplexer_10 (
    .in0(1'b0), .in1(multiplexer_9_out[31]), .out(multiplexer_10_out[7]), .sel(A_L));
  Multiplexer #(.width(8), .enable("false")) multiplexer_11 (
    .in0({8{1'b0}}), .in1(multiplexer_9_out[31:24]), .out(multiplexer_11_out), .sel(A_L));
  Multiplexer #(.select(2), .width(32), .enable("false")) multiplexer_12 (
    .in0(multiplexer_9_out), .in1(multiplexer_9_out),
    .in2({{8{multiplexer_10_out[7]}}, multiplexer_9_out[31:8]}),
    .in3({multiplexer_9_out[23:0], multiplexer_11_out}), .out(multiplexer_12_out), .sel({shamt[3], L_R}));
  Multiplexer #(.enable("false")) multiplexer_13 (
    .in0(1'b0), .in1(multiplexer_12_out[31]), .out(multiplexer_13_out[7]), .sel(A_L));
  Multiplexer #(.width(16), .enable("false")) multiplexer_14 (
    .in0({16{1'b0}}), .in1(multiplexer_12_out[31:16]), .out(multiplexer_14_out), .sel(A_L));
  Multiplexer #(.select(2), .width(32), .enable("false")) multiplexer_15 (
    .in0(multiplexer_12_out), .in1(multiplexer_12_out),
    .in2({{16{multiplexer_13_out[7]}}, multiplexer_12_out[31:16]}),
    .in3({multiplexer_12_out[15:0], multiplexer_14_out}), .out(DataOut), .sel({shamt[4], L_R}));

  // Other names for the same wires on the sheet: Din[31:0] = DataIn; Left_Right = L_R; Arth_Logic = A_L;
  //   Dout[31:0] = DataOut

  // Notes on the sheet:
  //   L/R,A/L: 00逻辑右移，01算术右移，10逻辑左移，11：循环左移
  //   输入引脚
  //   请勿修改引脚名称、电路名称及电路封装外观
  //   提示：使用多路选择器、逻辑门实现32位桶形移位器，禁止直接使用移位器组件。
  //   L:sign R:0
  //   3 right 4 left
  //   输出引脚
endmodule
