// Logisim project lab2.5.circ as structural Verilog: 1 circuit, main circuit main
module main (
  input  [7:0] DataIn,
  input  [2:0] shamt,
  input  L_R,
  input  A_L,
  output [7:0] DataOut
);

  wire not_1_out, not_2_out;
  wire [0:0] multiplexer_1_out, multiplexer_4_out;
  wire [7:0] multiplexer_2_out, multiplexer_5_out, multiplexer_10_out;
  wire [7:7] multiplexer_3_out;

  Multiplexer #(.enable("false")) multiplexer_1 (
    .in0(DataIn[7]), .in1(1'b0), .out(multiplexer_1_out[0]), .sel(not_1_out));
  not not_1 (not_1_out, A_L);
  Multiplexer #(.select(2), .width(8), .enable("false")) multiplexer_2 (
    .in0(DataIn), .in1(DataIn), .in2({multiplexer_1_out[0], DataIn[7:1]}),
    .in3({DataIn[6:0], multiplexer_1_out[0]}), .out(multiplexer_2_out), .sel({shamt[0], L_R}));
  Multiplexer #(.enable("false")) multiplexer_3 (
    .in0(1'b0), .in1(multiplexer_2_out[7]), .out(multiplexer_3_out[7]), .sel(A_L));
  Multiplexer #(.enable("false")) multiplexer_4 (
    .in0(1'b0), .in1(multiplexer_2_out[6]), .out(multiplexer_4_out[0]), .sel(A_L));
  Multiplexer #(.select(2), .width(8), .enable("false")) multiplexer_5 (
    .in0(multiplexer_2_out), .in1(multiplexer_2_out),
    .in2({{2{multiplexer_3_out[7]}}, multiplexer_2_out[7:2]}),
    .in3({multiplexer_2_out[5:0], multiplexer_3_out[7], multiplexer_4_out[0]}),
    .out({multiplexer_5_out[3:0], multiplexer_10_out[7:4]}), .sel({shamt[1], L_R}));
  not not_2 (not_2_out, A_L);
  Multiplexer #(.enable("false")) multiplexer_6 (
    .in0(multiplexer_5_out[3]), .in1(1'b0), .out(multiplexer_5_out[7]), .sel(not_2_out));
  Multiplexer #(.enable("false")) multiplexer_7 (
    .in0(1'b0), .in1(multiplexer_5_out[2]), .out(multiplexer_10_out[2]), .sel(A_L));
  Multiplexer #(.select(2), .width(8), .enable("false")) multiplexer_8 (
    .in0({multiplexer_5_out[3:0], multiplexer_10_out[7:4]}),
    .in1({multiplexer_5_out[3:0], multiplexer_10_out[7:4]}),
    .in2({{4{multiplexer_5_out[7]}}, multiplexer_5_out[3:0]}),
    .in3({multiplexer_10_out[7:4], multiplexer_5_out[7], multiplexer_10_out[2:0]}), .out(DataOut),
    .sel({shamt[2], L_R}));
  Multiplexer #(.enable("false")) multiplexer_9 (
    .in0(1'b0), .in1(multiplexer_5_out[1]), .out(multiplexer_10_out[1]), .sel(A_L));
  Multiplexer #(.enable("false")) multiplexer_10 (
    .in0(1'b0), .in1(multiplexer_5_out[0]), .out(multiplexer_10_out[0]), .sel(A_L));

  // Other names for the same wires on the sheet: Din[7:0] = DataIn; Left_Right = L_R; Arth_Logic = A_L;
  //   Dout[7:0] = DataOut

  // Notes on the sheet:
  //   0 is logic
  //   L/R,A/L: 00逻辑右移，01算术右移，10逻辑左移，11：循环左移
  //   输入引脚
  //   请勿修改引脚名称、电路名称及电路封装外观
  //   提示：使用多路选择器级联实现8位桶形移位器，禁止直接使用移位器组件。
  //   right
  //   left
  //   right if high
  //   输出引脚
endmodule
