// Logisim project lab4.5.circ as structural Verilog: 2 circuits, main circuit ALU
module ALU (
  input  [3:0] ALUctr,
  input  [31:0] A,
  input  [31:0] B,
  output Zero,
  output [31:0] S
);

  wire aluctrl_1_alctr, aluctrl_1_sftctr, aluctrl_1_sigctr, aluctrl_1_subctr, main_2_cf, main_2_of,
       main_2_sf, multiplexer_2_out, xor_2_out;
  wire [2:0] aluctrl_1_opctr;
  wire [31:0] _000, _001, _010, _011, _100, _110, multiplexer_1_out, not_1_out;

  assign _001 = A & B;  // AND_Gate and_1, 32 bits wide
  assign _010 = A | B;  // OR_Gate or_1, 32 bits wide
  assign _011 = A ^ B;  // XOR_Gate xor_1, 32 bits wide
  lab4_4_main main_1 (.L_R(aluctrl_1_sftctr), .shamt(B[4:0]), .DataIn(A), .DataOut(_100), .A_L(aluctrl_1_alctr));
  assign not_1_out = ~B;  // NOT_Gate not_1, 32 bits wide
  Multiplexer #(.width(32), .enable("false")) multiplexer_1 (
    .in0(B), .in1(not_1_out), .out(multiplexer_1_out), .sel(aluctrl_1_subctr));
  lab4_3_main main_2 (
    .Cin(aluctrl_1_subctr), .X(A), .Y(multiplexer_1_out), .S(_000), .OF(main_2_of), .CF(main_2_cf),
    .ZF(Zero), .SF(main_2_sf));  // open: Cout
  ALUctrl aluctrl_1 (
    .ALUctr(ALUctr), .SUBctr(aluctrl_1_subctr), .SFTctr(aluctrl_1_sftctr), .SIGctr(aluctrl_1_sigctr),
    .ALctr(aluctrl_1_alctr), .OPctr(aluctrl_1_opctr));
  Multiplexer #(.enable("false")) multiplexer_2 (
    .in0(main_2_cf), .in1(xor_2_out), .out(multiplexer_2_out), .sel(aluctrl_1_sigctr));
  xor xor_2 (xor_2_out, main_2_of, main_2_sf);
  // Probe on A
  // Probe on B
  // Probe on S
  assign _110 = {{31{1'b0}}, multiplexer_2_out};  // Bit_Extender bit_extender_1
  Multiplexer #(.select(3), .width(32), .enable("false")) multiplexer_3 (
    .in0(_000), .in1(_001), .in2(_010), .in3(_011), .in4(_100), .in5(B), .in6(_110), .out(S),
    .sel(aluctrl_1_opctr));  // open: in7

  // Other names for the same wires on the sheet: _101[31:0] = B; Result[31:0] = S

  // Notes on the sheet:
  //   ALUctr: pull=down
  //   A: pull=down
  //   B: pull=down
  //   输入引脚
  //   请勿修改引脚名称、电路名称及电路封装外观
  //   提示：使用32位并行加法器子电路、桶形移位器、ALU控制子电路实现32位ALU
  //   功能说明:32位ALU，输入32位操作数A、B，4位控制信号ALUctr，输出32位结果Reseult和1位Zero标志位
  //   输出引脚
  //   操作数和结果
endmodule

// ALU操作控制信号
module ALUctrl (
  input  [3:0] ALUctr,
  output SUBctr,
  output SFTctr,
  output SIGctr,
  output ALctr,
  output [2:0] OPctr
);

  wire and_1_out, and_2_out, and_3_out, and_4_out, and_5_out, and_6_out, and_7_out, and_8_out, and_9_out,
       and_10_out, buffer_1_out, buffer_2_out, buffer_3_out, buffer_4_out, not_1_out, not_2_out, not_3_out,
       not_4_out;

  buf buffer_1 (buffer_1_out, ALUctr[3]);
  not not_1 (not_1_out, ALUctr[3]);
  buf buffer_2 (buffer_2_out, ALUctr[0]);
  buf buffer_3 (buffer_3_out, ALUctr[1]);
  buf buffer_4 (buffer_4_out, ALUctr[2]);
  not not_2 (not_2_out, ALUctr[0]);
  not not_3 (not_3_out, ALUctr[2]);
  not not_4 (not_4_out, ALUctr[1]);
  and and_1 (and_1_out, not_2_out, buffer_3_out, not_3_out, not_1_out);
  and and_2 (and_2_out, buffer_2_out, buffer_3_out, not_3_out, not_1_out);
  and and_3 (and_3_out, not_2_out, not_4_out, not_3_out, buffer_1_out);
  and and_4 (and_4_out, buffer_2_out, not_4_out, buffer_4_out, buffer_1_out);
  and and_5 (and_5_out, buffer_2_out, not_4_out, not_3_out, not_1_out);
  and and_6 (and_6_out, buffer_2_out, not_4_out, buffer_4_out, not_1_out);
  and and_7 (and_7_out, buffer_2_out, buffer_3_out, buffer_4_out, buffer_1_out);
  and and_8 (and_8_out, not_2_out, not_4_out, buffer_4_out, not_1_out);
  and and_9 (and_9_out, not_2_out, buffer_3_out, buffer_4_out, not_1_out);
  and and_10 (and_10_out, buffer_2_out, buffer_3_out, buffer_4_out, not_1_out);
  buf buffer_5 (SIGctr, and_1_out);
  or or_1 (SUBctr, and_1_out, and_2_out, and_3_out);
  buf buffer_6 (ALctr, and_4_out);
  buf buffer_7 (SFTctr, and_5_out);
  or or_2 (OPctr[2], and_1_out, and_2_out, and_4_out, and_5_out, and_6_out, and_7_out);
  or or_3 (OPctr[1], and_1_out, and_2_out, and_8_out, and_9_out);
  or or_4 (OPctr[0], and_7_out, and_8_out, and_10_out);

  // Other names for the same wires on the sheet: LRctr = SFTctr

  // Notes on the sheet:
  //   输入引脚
  //   ALU操作控制信号生成部件
  //   输出引脚
endmodule
