// Logisim project lab5.2.circ as structural Verilog: 2 circuits, main circuit DataRam
// DataRAM
module DataRam (
  input  CLK,
  input  CLR,
  input  WE,
  input  [2:0] MemOp,
  input  [17:0] Addr,
  input  [31:0] Din,
  output AlignErr,
  output [31:0] DataOut
);

  wire s0, s1, s2, s3;
  wire [7:0] d0, d1, d2, d3, multiplexer_3_out, multiplexer_4_out;
  wire [15:0] multiplexer_5_out, multiplexer_6_out;
  wire [17:0] A;
  wire [31:0] _000, _001, _010, _101, _110;

  Multiplexer #(.select(3), .width(32), .enable("false")) multiplexer_1 (
    .in0(_000), .in1(_001), .in2(_010), .in5(_101), .in6(_110), .out(DataOut), .sel(MemOp));  // open: in3, in4, in7
  RAM #(.addrWidth(18), .bus("separate"), .Select("high")) ram_1 (
    .addr(A), .din(d3), .data(_000[31:24]), .str(WE), .sel(s3), .clk(CLK), .clr(CLR));  // open: ld
  opGen opgen_1 (
    .m2(MemOp[2]), .m1(MemOp[1]), .m0(MemOp[0]), .a1(Addr[1]), .a0(Addr[0]), .s3(s3), .s2(s2), .s1(s1),
    .s0(s0), .err(AlignErr));
  RAM #(.addrWidth(18), .bus("separate"), .Select("high")) ram_2 (
    .addr(A), .din(d2), .data(_000[23:16]), .str(WE), .sel(s2), .clk(CLK), .clr(CLR));  // open: ld
  Multiplexer #(.select(3), .width(32), .enable("false")) multiplexer_2 (
    .in0(Din), .in1({Din[7:0], Din[7:0], Din[7:0], Din[7:0]}), .in2({Din[15:0], Din[15:0]}),
    .in5({Din[7:0], Din[7:0], Din[7:0], Din[7:0]}), .in6({Din[15:0], Din[15:0]}), .out({d3, d2, d1, d0}),
    .sel(MemOp));  // open: in3, in4, in7
  Shifter #(.width(18), .shift("lr")) shifter_1 (.in(Addr), .\dist (5'b00010), .out(A));
  assign _001 = {{24{1'b0}}, multiplexer_3_out};  // Bit_Extender bit_extender_1
  Multiplexer #(.select(2), .width(8), .enable("false")) multiplexer_3 (
    .in0(_000[7:0]), .in1(_000[15:8]), .in2(_000[23:16]), .in3(_000[31:24]), .out(multiplexer_3_out),
    .sel(Addr[1:0]));
  assign _101 = {{24{multiplexer_4_out[7]}}, multiplexer_4_out};  // Bit_Extender bit_extender_2
  Multiplexer #(.select(2), .width(8), .enable("false")) multiplexer_4 (
    .in0(_000[7:0]), .in1(_000[15:8]), .in2(_000[23:16]), .in3(_000[31:24]), .out(multiplexer_4_out),
    .sel(Addr[1:0]));
  RAM #(.addrWidth(18), .bus("separate"), .Select("high")) ram_3 (
    .addr(A), .din(d1), .data(_000[15:8]), .str(WE), .sel(s1), .clk(CLK), .clr(CLR));  // open: ld
  Multiplexer #(.select(2), .width(16), .enable("false")) multiplexer_5 (
    .in0(_000[15:0]), .in2(_000[31:16]), .out(multiplexer_5_out), .sel(Addr[1:0]));  // open: in1, in3
  Multiplexer #(.select(2), .width(16), .enable("false")) multiplexer_6 (
    .in0(_000[15:0]), .in2(_000[31:16]), .out(multiplexer_6_out), .sel(Addr[1:0]));  // open: in1, in3
  RAM #(.addrWidth(18), .bus("separate"), .Select("high")) ram_4 (
    .addr(A), .din(d0), .data(_000[7:0]), .str(WE), .sel(s0), .clk(CLK), .clr(CLR));  // open: ld
  assign _010 = {{16{1'b0}}, multiplexer_5_out};  // Bit_Extender bit_extender_3
  assign _110 = {{16{multiplexer_6_out[15]}}, multiplexer_6_out};  // Bit_Extender bit_extender_4

  // Other names for the same wires on the sheet: dd0[7:0] = Din[7:0]; dd1[7:0] = Din[15:8]; o0[7:0] = _000[7:0];
  //   o1[7:0] = _000[15:8]; o2[7:0] = _000[23:16]; o3[7:0] = _000[31:24]; Data[31:0] = {d3, d2, d1, d0};
  //   dd2[7:0] = Din[23:16]; dd3[7:0] = Din[31:24]; Dout[31:0] = DataOut

  // Notes on the sheet:
  //   输入引脚
  //   请勿修改引脚名称、电路名称及电路封装外观
  //   为了后续实验中的引用，不要修改MemOp的编码定义、引脚名称和在布局中的位置。
  //   32位数据存储器，按字节分4片存储，可按照字节、半字和字进行存储；读取字节或半字时，支持0扩展和符号位扩展。
  //   输出引脚
endmodule

module opGen (
  input  m2,
  input  m1,
  input  m0,
  input  a1,
  input  a0,
  output s3,
  output s2,
  output s1,
  output s0,
  output err
);

  wire nand_1_out, nand_2_out, nand_3_out, nand_4_out, nand_5_out, nand_6_out, nand_7_out, nand_8_out,
       nand_9_out, nand_10_out, nand_11_out, nand_12_out, nand_13_out, nand_14_out, nand_15_out, nand_16_out,
       nand_17_out, nand_18_out, nand_19_out, nand_20_out, nand_21_out, nand_22_out, nand_23_out,
       nand_24_out, nand_25_out, nand_26_out, nand_27_out, nand_28_out, nand_29_out, nand_30_out,
       nand_31_out, nand_32_out, nand_33_out, nand_34_out, nand_35_out, nand_36_out, nand_37_out,
       nand_38_out, nand_39_out, nand_40_out, nand_41_out, nand_42_out, nand_43_out, nand_44_out,
       nand_45_out, nand_46_out, nand_47_out, nand_48_out, nand_49_out, nand_50_out, nand_51_out,
       nand_52_out, nand_53_out, nand_54_out, nand_55_out, nand_56_out, nand_57_out, nand_58_out,
       nand_59_out, nand_60_out, nand_61_out, nand_62_out, nand_63_out, nand_64_out, nand_65_out,
       nand_66_out, nand_67_out, nand_68_out, nand_69_out, nand_70_out, nand_71_out, nand_72_out,
       nand_73_out, nand_74_out, nand_75_out, nand_76_out, nand_77_out, nand_78_out, nand_79_out,
       nand_80_out, nand_81_out, nand_82_out, nand_83_out, nand_84_out, nand_85_out, nand_86_out,
       nand_87_out, nand_88_out, nand_89_out, nand_90_out, nand_91_out, nand_92_out, nand_93_out,
       nand_94_out, nand_95_out, nand_96_out, nand_97_out, nand_98_out, nand_99_out, nand_100_out,
       nand_101_out, nand_102_out, nand_103_out, nand_104_out, nand_105_out, nand_106_out, nand_107_out,
       nand_108_out, nand_109_out, nand_110_out, nand_111_out, nand_112_out, nand_113_out, nand_114_out,
       nand_115_out, nand_116_out, nand_117_out, nand_118_out, nand_119_out, nand_120_out, nand_121_out,
       nand_125_out, nand_126_out, nand_127_out, nand_128_out;

  nand nand_1 (nand_1_out, m2, m2);
  nand nand_2 (nand_2_out, m1, m1);
  nand nand_3 (nand_3_out, m2, m2);
  nand nand_4 (nand_4_out, m1, m1);
  nand nand_5 (nand_5_out, m2, m2);
  nand nand_6 (nand_6_out, m0, m0);
  nand nand_7 (nand_7_out, a1, a1);
  nand nand_8 (nand_8_out, a0, a0);
  nand nand_9 (nand_9_out, m1, m1);
  nand nand_10 (nand_10_out, a1, a1);
  nand nand_11 (nand_11_out, m2, m2);
  nand nand_12 (nand_12_out, m1, m1);
  nand nand_13 (nand_13_out, a1, a1);
  nand nand_14 (nand_14_out, a0, a0);
  nand nand_15 (nand_15_out, m1, m1);
  nand nand_16 (nand_16_out, a1, a1);
  nand nand_17 (nand_17_out, a0, a0);
  nand nand_18 (nand_18_out, m1, m1);
  nand nand_19 (nand_19_out, m0, m0);
  nand nand_20 (nand_20_out, m1, m1);
  nand nand_21 (nand_21_out, nand_1_out, nand_2_out);
  nand nand_22 (nand_22_out, nand_3_out, nand_4_out);
  nand nand_23 (nand_23_out, nand_5_out, nand_6_out);
  nand nand_24 (nand_24_out, nand_7_out, nand_8_out);
  nand nand_25 (nand_25_out, nand_9_out, m0);
  nand nand_26 (nand_26_out, nand_10_out, a0);
  nand nand_27 (nand_27_out, nand_11_out, nand_12_out);
  nand nand_28 (nand_28_out, nand_13_out, nand_14_out);
  nand nand_29 (nand_29_out, nand_15_out, m0);
  nand nand_30 (nand_30_out, nand_16_out, nand_17_out);
  nand nand_31 (nand_31_out, nand_18_out, nand_19_out);
  nand nand_32 (nand_32_out, m2, nand_20_out);
  nand nand_33 (nand_33_out, nand_21_out, nand_21_out);
  nand nand_34 (nand_34_out, m0, m0);
  nand nand_35 (nand_35_out, a1, a1);
  nand nand_36 (nand_36_out, a0, a0);
  nand nand_37 (nand_37_out, m1, m1);
  nand nand_38 (nand_38_out, nand_22_out, nand_22_out);
  nand nand_39 (nand_39_out, m0, m0);
  nand nand_40 (nand_40_out, a1, a1);
  nand nand_41 (nand_41_out, a0, a0);
  nand nand_42 (nand_42_out, m1, m1);
  nand nand_43 (nand_43_out, a0, a0);
  nand nand_44 (nand_44_out, nand_23_out, nand_23_out);
  nand nand_45 (nand_45_out, nand_24_out, nand_24_out);
  nand nand_46 (nand_46_out, nand_25_out, nand_25_out);
  nand nand_47 (nand_47_out, nand_26_out, nand_26_out);
  nand nand_48 (nand_48_out, m0, m0);
  nand nand_49 (nand_49_out, a1, a1);
  nand nand_50 (nand_50_out, a0, a0);
  nand nand_51 (nand_51_out, nand_27_out, nand_27_out);
  nand nand_52 (nand_52_out, nand_28_out, nand_28_out);
  nand nand_53 (nand_53_out, nand_29_out, nand_29_out);
  nand nand_54 (nand_54_out, nand_30_out, nand_30_out);
  nand nand_55 (nand_55_out, m0, m0);
  nand nand_56 (nand_56_out, a1, a1);
  nand nand_57 (nand_57_out, a0, a0);
  nand nand_58 (nand_58_out, m0, m0);
  nand nand_59 (nand_59_out, nand_31_out, nand_31_out);
  nand nand_60 (nand_60_out, nand_32_out, nand_32_out);
  nand nand_61 (nand_61_out, m0, m0);
  nand nand_62 (nand_62_out, nand_33_out, nand_34_out);
  nand nand_63 (nand_63_out, nand_35_out, nand_36_out);
  nand nand_64 (nand_64_out, nand_37_out, m0);
  nand nand_65 (nand_65_out, a1, a0);
  nand nand_66 (nand_66_out, nand_38_out, nand_39_out);
  nand nand_67 (nand_67_out, nand_40_out, nand_41_out);
  nand nand_68 (nand_68_out, nand_42_out, m0);
  nand nand_69 (nand_69_out, a1, nand_43_out);
  nand nand_70 (nand_70_out, nand_44_out, nand_45_out);
  nand nand_71 (nand_71_out, nand_46_out, nand_47_out);
  nand nand_72 (nand_72_out, m1, nand_48_out);
  nand nand_73 (nand_73_out, nand_49_out, nand_50_out);
  nand nand_74 (nand_74_out, nand_51_out, nand_52_out);
  nand nand_75 (nand_75_out, nand_53_out, nand_54_out);
  nand nand_76 (nand_76_out, m1, nand_55_out);
  nand nand_77 (nand_77_out, nand_56_out, nand_57_out);
  nand nand_78 (nand_78_out, nand_58_out, a0);
  nand nand_79 (nand_79_out, nand_59_out, a1);
  nand nand_80 (nand_80_out, m1, m0);
  nand nand_81 (nand_81_out, nand_60_out, nand_61_out);
  nand nand_82 (nand_82_out, nand_62_out, nand_62_out);
  nand nand_83 (nand_83_out, nand_63_out, nand_63_out);
  nand nand_84 (nand_84_out, nand_64_out, nand_64_out);
  nand nand_85 (nand_85_out, nand_65_out, nand_65_out);
  nand nand_86 (nand_86_out, m0, m0);
  nand nand_87 (nand_87_out, a0, a0);
  nand nand_88 (nand_88_out, nand_66_out, nand_66_out);
  nand nand_89 (nand_89_out, nand_67_out, nand_67_out);
  nand nand_90 (nand_90_out, nand_68_out, nand_68_out);
  nand nand_91 (nand_91_out, nand_69_out, nand_69_out);
  nand nand_92 (nand_92_out, m0, m0);
  nand nand_93 (nand_93_out, a0, a0);
  nand nand_94 (nand_94_out, nand_70_out, nand_71_out);
  nand nand_95 (nand_95_out, nand_72_out, nand_72_out);
  nand nand_96 (nand_96_out, nand_73_out, nand_73_out);
  nand nand_97 (nand_97_out, nand_74_out, nand_75_out);
  nand nand_98 (nand_98_out, nand_76_out, nand_76_out);
  nand nand_99 (nand_99_out, nand_77_out, nand_77_out);
  nand nand_100 (nand_100_out, nand_78_out, nand_79_out);
  nand nand_101 (nand_101_out, nand_80_out, nand_81_out);
  nand nand_102 (nand_102_out, nand_82_out, nand_83_out);
  nand nand_103 (nand_103_out, nand_84_out, nand_85_out);
  nand nand_104 (nand_104_out, m1, nand_86_out);
  nand nand_105 (nand_105_out, a1, nand_87_out);
  nand nand_106 (nand_106_out, nand_88_out, nand_89_out);
  nand nand_107 (nand_107_out, nand_90_out, nand_91_out);
  nand nand_108 (nand_108_out, m1, nand_92_out);
  nand nand_109 (nand_109_out, a1, nand_93_out);
  nand nand_110 (nand_110_out, nand_94_out, nand_94_out);
  nand nand_111 (nand_111_out, nand_95_out, nand_96_out);
  nand nand_112 (nand_112_out, nand_97_out, nand_97_out);
  nand nand_113 (nand_113_out, nand_98_out, nand_99_out);
  nand nand_114 (nand_114_out, nand_100_out, nand_100_out);
  nand nand_115 (nand_115_out, nand_101_out, nand_101_out);
  nand nand_116 (nand_116_out, nand_102_out, nand_103_out);
  nand nand_117 (nand_117_out, nand_104_out, nand_104_out);
  nand nand_118 (nand_118_out, nand_105_out, nand_105_out);
  nand nand_119 (nand_119_out, nand_106_out, nand_107_out);
  nand nand_120 (nand_120_out, nand_108_out, nand_108_out);
  nand nand_121 (nand_121_out, nand_109_out, nand_109_out);
  nand nand_122 (s1, nand_110_out, nand_111_out);
  nand nand_123 (s0, nand_112_out, nand_113_out);
  nand nand_124 (err, nand_114_out, nand_115_out);
  nand nand_125 (nand_125_out, nand_116_out, nand_116_out);
  nand nand_126 (nand_126_out, nand_117_out, nand_118_out);
  nand nand_127 (nand_127_out, nand_119_out, nand_119_out);
  nand nand_128 (nand_128_out, nand_120_out, nand_121_out);
  nand nand_129 (s3, nand_125_out, nand_126_out);
  nand nand_130 (s2, nand_127_out, nand_128_out);
endmodule
