// Logisim project lab5.5.circ as structural Verilog: 3 circuits, main circuit main
module main (
  input  [2:0] ExtOp,
  input  [2:0] MemOp,
  input  RegWr,
  input  ALUASrc,
  input  MemWr,
  input  [1:0] ALUBSrc,
  input  [31:0] Initial_Address,
  input  [3:0] ALUctr,
  input  MemToReg,
  input  [2:0] Branch,
  input  clk,
  input  ReSet,
  output [31:0] PC,
  output [31:0] Din,
  output [31:0] BusW,
  output NxtASrc,
  output NxtBSrc
);

  wire alu_1_zero;
  wire [15:0] ifu_1_addr;
  wire [31:0] dataram_1_dataout, idu_1_busa, idu_1_dataa, idu_1_datab, idu_1_imm, rom_1_data, S;

  IFU ifu_1 (
    .CLK(clk), .Reset(ReSet), .NxtASrc(NxtASrc), .NxtBSrc(NxtBSrc), .Initial_Address(Initial_Address),
    .Imm(idu_1_imm), .BusA(idu_1_busa), .PC(PC), .addr(ifu_1_addr));
  ROM #(.addrWidth(16), .dataWidth(32), .Select("low")) rom_1 (.addr(ifu_1_addr), .data(rom_1_data), .sel(ReSet));
  IDU idu_1 (
    .ExtOp(ExtOp), .RegWr(RegWr), .ALUASrc(ALUASrc), .ALUBSrc(ALUBSrc), .BusW(BusW), .PC(PC),
    .DataA(idu_1_dataa), .BusB(Din), .DataB(idu_1_datab), .Imm(idu_1_imm), .BusA(idu_1_busa), .CLK(clk),
    .IR(rom_1_data));  // open: OpCode, Funct3, Funct7
  ALU alu_1 (.A(idu_1_dataa), .B(idu_1_datab), .S(S), .ALUctr(ALUctr), .Zero(alu_1_zero));
  Branch branch_1 (.Branch(Branch), .NxtASrc(NxtASrc), .Zero(alu_1_zero), .NxtBSrc(NxtBSrc), .Result0(S[0]));
  DataRam dataram_1 (
    .Addr(S[17:0]), .Din(Din), .DataOut(dataram_1_dataout), .CLK(clk), .CLR(ReSet), .MemOp(MemOp), .WE(MemWr));  // open: AlignErr
  Multiplexer #(.width(32), .enable("false")) multiplexer_1 (
    .in0(S), .in1(dataram_1_dataout), .out(BusW), .sel(MemToReg));

  // Other names for the same wires on the sheet: Init_Addr[31:0] = Initial_Address

  // Notes on the sheet:
  //   RegWr: pull=down
  //   NxtASrc: pull=down
  //   ALUctr: pull=down
  //   NxtBSrc: pull=down
  //   ALUASrc: pull=down
  //   Branch: pull=down
  //   ALUBSrc: pull=down
  //   ExtOp: pull=down
  //   输入信号
  //   contents of rom_1 (hex, n*v repeats v):
  //   256*0 fedca2b7 f9c28293 1006013 6502223 6400303 6601423 6405383 6701623 4042d413 6444b3 649533
  //   8505b3 b2a633 b2b6b3 40b287b3 6f02823 67c263 67d263 40086f 4808e7 1917
  //   请勿修改引脚名称、电路名称及电路封装外观
  //   为了后续实验中的引用，不要修改控制信号的编码定义、引脚名称和在布局中的位置。
  //   指令存储器和数据存储器数据位都是32位，指令存储器编址以字为单位，数据存储器编址以字节为单位。
  //   32位数据存储器，按字节分4片存储，可按照字节、半字和字进行存储；读取字节或半字时，支持0扩展和符号位扩展。
  //   输出信号
endmodule

module Branch (
  input  [2:0] Branch,
  input  Zero,
  input  Result0,
  output NxtASrc,
  output NxtBSrc
);

  wire not_1_out, or_1_out;

  and and_1 (NxtASrc, ~Branch[0], Branch[1], ~Branch[2]);  // AND_Gate
  Multiplexer #(.select(3), .enable("false")) multiplexer_1 (
    .in0(1'b0), .in1(1'b1), .in2(1'b1), .in4(Zero), .in5(not_1_out), .in6(Result0), .in7(or_1_out),
    .out(NxtBSrc), .sel(Branch));  // open: in3
  not not_1 (not_1_out, Zero);
  or or_1 (or_1_out, Zero, ~Result0);  // OR_Gate

  // Notes on the sheet:
  //   Branch: pull=down
  //   Zero: pull=down
  //   输入信号
  //   请勿修改引脚名称、电路名称及电路封装外观
  //   不要修改控制信号的编码定义、引脚名称和在布局中的位置。
  //   输出信号
endmodule

module IFU (
  input  [31:0] Initial_Address,
  input  [31:0] Imm,
  input  [31:0] BusA,
  input  CLK,
  input  Reset,
  input  NxtASrc,
  input  NxtBSrc,
  output [31:0] PC,
  output [15:0] addr
);

  wire [31:0] adder_1_out, multiplexer_1_out, multiplexer_2_out, multiplexer_3_out;

  Multiplexer #(.width(32), .enable("false")) multiplexer_1 (
    .in0({PC[31:18], addr, PC[1:0]}), .in1(BusA), .out(multiplexer_1_out), .sel(NxtASrc));
  Multiplexer #(.width(32), .enable("false")) multiplexer_2 (
    .in0(32'h4), .in1(Imm), .out(multiplexer_2_out), .sel(NxtBSrc));
  Adder #(.width(32)) adder_1 (
    .a(multiplexer_1_out), .b(multiplexer_2_out), .out(adder_1_out), .cin(1'b0));  // open: cout
  Multiplexer #(.width(32), .enable("false")) multiplexer_3 (
    .in0(adder_1_out), .in1(Initial_Address), .out(multiplexer_3_out), .sel(Reset));
  Register #(.width(32), .Select("low")) u_PC (
    .D(multiplexer_3_out), .Q({PC[31:18], addr, PC[1:0]}), .clk(CLK));  // open: en, clr

  assign PC[17:2] = addr;

  // Other names for the same wires on the sheet: Init_Addr[31:0] = Initial_Address

  // Notes on the sheet:
  //   NxtASrc: pull=down
  //   NxtBSrc: pull=down
  //   BusA: pull=down
  //   Imm: pull=down
  //   输入信号
  //   请勿修改引脚名称、电路名称及电路封装外观
  //   指令存储器256KB，数据位为32位，地址位为16位。PC寄存器数据宽度32位，片选信号高电平有效
  //   输出信号
endmodule
