// Logisim project lab6.1.circ as structural Verilog: 9 circuits, main circuit 控制器
module \控制器  (
  input  [6:0] opcode,
  input  [2:0] funct3,
  input  [6:0] funct7,
  output [2:0] ExtOp,
  output RegWr,
  output [2:0] Branch,
  output ALUASrc,
  output [1:0] ALUBSrc,
  output [3:0] ALUctr,
  output MemtoReg,
  output [2:0] MemOp,
  output MemWr
);

  wire and_1_out, and_2_out, halt, I_Arith, J_jal, J_jalr, or_1_out, or_8_out, R_Arith, U_auipc, U_lui;

  Comparator #(.width(7)) comparator_1 (.a(opcode), .b(7'b0110111), .eq(U_lui));  // open: gt, lt
  Comparator #(.width(7)) comparator_2 (.a(opcode), .b(7'b1100111), .eq(J_jalr));  // open: gt, lt
  Comparator #(.width(7)) comparator_3 (.a(opcode), .b(7'b0010111), .eq(U_auipc));  // open: gt, lt
  Comparator #(.width(7)) comparator_4 (.a(opcode), .b(7'b1100011), .eq(Branch[2]));  // open: gt, lt
  Comparator #(.width(7)) comparator_5 (.a(opcode), .b(7'b0010011), .eq(I_Arith));  // open: gt, lt
  Comparator #(.width(7)) comparator_6 (.a(opcode), .b(7'b0000011), .eq(MemtoReg));  // open: gt, lt
  or or_1 (or_1_out, U_lui, U_auipc);
  or or_2 (ALUBSrc[0], J_jal, J_jalr);
  and and_1 (and_1_out, Branch[2], funct3[2]);
  and and_2 (and_2_out, Branch[2], funct3[0]);
  Comparator #(.width(7)) comparator_7 (.a(opcode), .b(7'b0110011), .eq(R_Arith));  // open: gt, lt
  Comparator #(.width(7)) comparator_8 (.a(opcode), .b(7'b0100011), .eq(MemWr));  // open: gt, lt
  or or_3 (Branch[1], and_1_out, J_jalr);
  or or_4 (Branch[0], J_jal, and_2_out);
  or or_5 (RegWr, or_1_out, ALUBSrc[0], I_Arith, R_Arith, MemtoReg);
  Comparator #(.width(7)) comparator_9 (.a(opcode), .b(7'b1101111), .eq(J_jal));  // open: gt, lt
  Comparator #(.width(7)) comparator_10 (.a(opcode), .b(7'b1110011), .eq(halt));  // open: gt, lt
  or or_6 (ALUASrc, U_auipc, ALUBSrc[0]);
  or or_7 (ALUBSrc[1], or_1_out, I_Arith, MemtoReg, MemWr);
  Extop extop_1 (
    .a(opcode[6]), .b(opcode[5]), .c(opcode[4]), .d(opcode[3]), .e(opcode[2]), .f(opcode[1]), .g(opcode[0]),
    .out_8(ExtOp[2]), .out_9(ExtOp[1]), .out_10(ExtOp[0]));
  or or_8 (or_8_out, funct7[5], 1'b0);
  mem2 mem2_1 (
    .in_1(opcode[6]), .in_2(opcode[5]), .in_3(opcode[4]), .in_4(opcode[3]), .in_5(opcode[2]),
    .in_6(opcode[1]), .in_7(opcode[0]), .in_8(funct3[2]), .in_9(funct3[1]), .in_10(funct3[0]),
    .out_11(MemOp[2]));
  mem1 mem1_1 (
    .in_1(opcode[6]), .in_2(opcode[5]), .in_3(opcode[4]), .in_4(opcode[3]), .in_5(opcode[2]),
    .in_6(opcode[1]), .in_7(opcode[0]), .in_8(funct3[2]), .in_9(funct3[1]), .in_10(funct3[0]),
    .out_11(MemOp[1]));
  Aluctr4 aluctr4_1 (
    ._6(opcode[6]), ._5(opcode[5]), ._4(opcode[4]), ._3(opcode[3]), ._2(opcode[2]), ._1(opcode[1]),
    ._0(opcode[0]), .fun32(funct3[2]), .fun31(funct3[1]), .fun30(funct3[0]), .fun75(or_8_out),
    .out_12(ALUctr[3]));
  Aluctr3 aluctr3_1 (
    ._6(opcode[6]), ._5(opcode[5]), ._4(opcode[4]), ._3(opcode[3]), ._2(opcode[2]), ._1(opcode[1]),
    ._0(opcode[0]), .fun2(funct3[2]), .fun1(funct3[1]), .fun0(funct3[0]), .fun75(or_8_out), .out_12(ALUctr[2]));
  Aluctr2 aluctr2_1 (
    ._6(opcode[6]), ._5(opcode[5]), ._4(opcode[4]), ._3(opcode[3]), ._2(opcode[2]), ._1(opcode[1]),
    ._0(opcode[0]), .func32(funct3[2]), .func31(funct3[1]), .fun30(funct3[0]), .in_11(or_8_out),
    .out_12(ALUctr[1]));
  Alutrc1 alutrc1_1 (
    ._6(opcode[6]), ._5(opcode[5]), ._4(opcode[4]), ._3(opcode[3]), ._2(opcode[2]), ._1(opcode[1]),
    ._0(opcode[0]), .fun32(funct3[2]), .fun31(funct3[1]), .fun30(funct3[0]), .fnu75(or_8_out),
    .out_12(ALUctr[0]));
  mem0 mem0_1 (
    .in_1(opcode[6]), .in_2(opcode[5]), .in_3(opcode[4]), .in_4(opcode[3]), .in_5(opcode[2]),
    .in_6(opcode[1]), .in_7(opcode[0]), .in_8(funct3[2]), .in_9(funct3[1]), .in_10(funct3[0]),
    .out_11(MemOp[0]));

  // Other names for the same wires on the sheet: B_Instr = Branch[2]; I_load = MemtoReg; S_Instr = MemWr

  // Notes on the sheet:
  //   输入引脚
  //   请勿修改引脚名称、电路名称及电路封装外观
  //   提示：根据指令种类，把7位指令code用一位指令类型标志位来表示，再通过功能码来区分具体指令，生成控制信号。
  //   输出引脚
endmodule

module Extop (
  input  a,
  input  b,
  input  c,
  input  d,
  input  e,
  input  f,
  input  g,
  output out_8,
  output out_9,
  output out_10
);

  wire and_1_out, and_2_out, and_3_out, or_1_out;

  and and_1 (and_1_out, ~a, b, c, e);  // AND_Gate
  and and_2 (and_2_out, ~a, ~b, c, e);  // AND_Gate
  and and_3 (and_3_out, a, b, ~c, ~e);  // AND_Gate
  or or_1 (or_1_out, and_1_out, and_2_out, and_3_out);
  and and_4 (out_8, a, b, d, e, f, g);
  and and_5 (out_9, b, ~d, ~c, ~e, f, g);  // AND_Gate
  and and_6 (out_10, or_1_out, ~d, f, g);  // AND_Gate
endmodule

module Aluctr4 (
  input  _6,
  input  _5,
  input  _4,
  input  _3,
  input  _2,
  input  _1,
  input  _0,
  input  fun32,
  input  fun31,
  input  fun30,
  input  fun75,
  output out_12
);

  wire _1_t, _2_t, _3_t, and_7_out, and_8_out, and_9_out, and_10_out, fun2, fun3, Other;

  and and_1 (fun2, fun32, ~fun31, fun30);  // AND_Gate
  and and_2 (fun3, ~fun32, ~fun31, ~fun30);  // AND_Gate
  and and_3 (Other, ~_6, _4, ~_3, _1, _0);  // AND_Gate
  and and_4 (_1_t, _5, _2);
  and and_5 (_2_t, ~_5, ~_2);  // AND_Gate
  and and_6 (_3_t, _5, ~_2);  // AND_Gate
  and and_7 (and_7_out, Other, _1_t);
  and and_8 (and_8_out, _2_t, Other, fun2, fun75);
  and and_9 (and_9_out, Other, _3_t, fun75, fun3);
  and and_10 (and_10_out, Other, fun2, _3_t, fun75);
  or or_1 (out_12, and_7_out, and_8_out, and_9_out, and_10_out);
endmodule

module Aluctr3 (
  input  _6,
  input  _5,
  input  _4,
  input  _3,
  input  _2,
  input  _1,
  input  _0,
  input  fun2,
  input  fun1,
  input  fun0,
  input  fun75,
  output out_12
);

  wire _1_t, _2_t, _3_t, and_1_out, and_10_out, and_11_out, and_12_out, fun21, fun22, fun31, fun32, func2,
       func3, not_1_out, other;

  and and_1 (and_1_out, ~fun1, fun0);  // AND_Gate
  and and_2 (other, ~_6, _4, _1, _0);  // AND_Gate
  and and_3 (_1_t, _5, ~_3, _2);  // AND_Gate
  and and_4 (_2_t, ~_5, ~_3, ~_2);  // AND_Gate
  and and_5 (_3_t, _5, ~_3, ~_2);  // AND_Gate
  and and_6 (fun21, fun2, not_1_out);
  not not_1 (not_1_out, and_1_out);
  and and_7 (fun22, fun2, ~fun1, fun0);  // AND_Gate
  and and_8 (fun31, fun2, ~fun75);  // AND_Gate
  and and_9 (fun32, fun2, ~fun1, fun0, fun75);  // AND_Gate
  or or_1 (func2, fun21, fun22);
  or or_2 (func3, fun31, fun32);
  and and_10 (and_10_out, other, _1_t);
  and and_11 (and_11_out, other, _2_t, func2);
  and and_12 (and_12_out, other, _3_t, func3);
  or or_3 (out_12, and_10_out, and_11_out, and_12_out);
endmodule

module Aluctr2 (
  input  _6,
  input  _5,
  input  _4,
  input  _3,
  input  _2,
  input  _1,
  input  _0,
  input  func32,
  input  func31,
  input  fun30,
  input  in_11,
  output out_12
);

  wire _1_t, _2_t, _3_t, _4_t, and_3_out, and_9_out, and_10_out, and_11_out, and_12_out, fun3, fun4, fun31,
       fun32, other;

  and and_1 (fun31, ~func32, func31, ~in_11);  // AND_Gate
  and and_2 (fun32, func32, func31, ~in_11);  // AND_Gate
  and and_3 (and_3_out, ~func32, ~func31);  // AND_Gate
  and and_4 (other, ~_3, _1, _0);  // AND_Gate
  or or_1 (fun4, func32, and_3_out);
  and and_5 (_1_t, ~_6, _5, _4, _2);  // AND_Gate
  and and_6 (_2_t, ~_6, ~_5, _4, ~_2);  // AND_Gate
  and and_7 (_3_t, ~_6, _5, _4, ~_2);  // AND_Gate
  and and_8 (_4_t, _6, _5, ~_4, ~_2);  // AND_Gate
  or or_2 (fun3, fun31, fun32);
  and and_9 (and_9_out, other, _1_t);
  and and_10 (and_10_out, other, _2_t, func31);
  and and_11 (and_11_out, other, _3_t, fun3);
  and and_12 (and_12_out, other, _4_t, fun4);
  or or_3 (out_12, and_9_out, and_10_out, and_11_out, and_12_out);

  // Other names for the same wires on the sheet: fun2 = func31
endmodule

module Alutrc1 (
  input  _6,
  input  _5,
  input  _4,
  input  _3,
  input  _2,
  input  _1,
  input  _0,
  input  fun32,
  input  fun31,
  input  fun30,
  input  fnu75,
  output out_12
);

  wire _1_t, _2_t, _3_t, _4_t, and_1_out, and_13_out, and_14_out, and_15_out, and_16_out, fun2, fun3, fun4,
       fun21, fun22, fun23, fun31_t, fun32_t, not_1_out, other;

  and and_1 (and_1_out, fun32, fun31);
  not not_1 (not_1_out, and_1_out);
  and and_2 (fun21, fun31, fun30);
  and and_3 (fun22, ~fun31, fun30, ~fnu75);  // AND_Gate
  and and_4 (fun23, fun32, ~fun31, fun30, fnu75);  // AND_Gate
  and and_5 (fun31_t, not_1_out, fun30, ~fnu75);  // AND_Gate
  and and_6 (fun4, fun32, fun31);
  and and_7 (fun32_t, fun32, fun31, fun30, ~fnu75);  // AND_Gate
  and and_8 (other, ~_3, _1, _0);  // AND_Gate
  and and_9 (_1_t, ~_6, _5, _4, _2);  // AND_Gate
  and and_10 (_2_t, ~_6, ~_5, _4, ~_2);  // AND_Gate
  and and_11 (_3_t, ~_6, _5, _4, ~_2);  // AND_Gate
  and and_12 (_4_t, _6, _5, ~_4, ~_2);  // AND_Gate
  or or_1 (fun2, fun21, fun22, fun23);
  or or_2 (fun3, fun23, fun31_t, fun32_t);
  and and_13 (and_13_out, other, _1_t);
  and and_14 (and_14_out, other, _2_t, fun2);
  and and_15 (and_15_out, other, _3_t, fun3);
  and and_16 (and_16_out, _4_t, other, fun4);
  or or_3 (out_12, and_13_out, and_14_out, and_15_out, and_16_out);
endmodule

module mem2 (
  input  in_1,
  input  in_2,
  input  in_3,
  input  in_4,
  input  in_5,
  input  in_6,
  input  in_7,
  input  in_8,
  input  in_9,
  input  in_10,
  output out_11
);

  and and_1 (out_11, ~in_1, ~in_3, ~in_4, ~in_5, in_6, in_7, ~in_8, ~in_9);  // AND_Gate
endmodule

module mem1 (
  input  in_1,
  input  in_2,
  input  in_3,
  input  in_4,
  input  in_5,
  input  in_6,
  input  in_7,
  input  in_8,
  input  in_9,
  input  in_10,
  output out_11
);

  wire and_1_out, and_2_out;

  and and_1 (and_1_out, ~in_1, ~in_3, ~in_4, ~in_5, in_6, in_7, ~in_8, ~in_9, in_10);  // AND_Gate
  and and_2 (and_2_out, ~in_1, ~in_2, ~in_3, ~in_4, ~in_5, in_6, in_7, in_8, ~in_9, in_10);  // AND_Gate
  or or_1 (out_11, and_1_out, and_2_out);
endmodule

module mem0 (
  input  in_1,
  input  in_2,
  input  in_3,
  input  in_4,
  input  in_5,
  input  in_6,
  input  in_7,
  input  in_8,
  input  in_9,
  input  in_10,
  output out_11
);

  wire and_1_out, and_2_out;

  and and_1 (and_1_out, ~in_1, ~in_2, ~in_3, ~in_4, ~in_5, in_6, in_7, ~in_9, ~in_10);  // AND_Gate
  and and_2 (and_2_out, ~in_1, in_2, ~in_3, ~in_4, ~in_5, in_6, in_7, ~in_8, ~in_9, ~in_10);  // AND_Gate
  or or_1 (out_11, and_1_out, and_2_out);
endmodule
