// Logisim project lab6.4.circ as structural Verilog: 6 circuits, main circuit main
module main (
  input  ReSet,
  input  [31:0] Init_Addr,
  input  clk,
  output [31:0] PC,
  output [31:0] IR,
  output [31:0] BusW,
  output [31:0] Din,
  output [15:0] Cycles,
  output Halt
);

  wire alu_1_zero, ALUASrc, clk_out, clk_t, MemToReg, MemWr, not_2_out, NxtASrc, NxtBSrc, RegWr;
  wire [1:0] ALUBSrc;
  wire [2:0] Branch, ExtOp, func3, MemOp;
  wire [3:0] ALUctr;
  wire [6:0] func7, opcode;
  wire [15:0] ifu_1_addr;
  wire [31:0] dataram_1_dataout, idu_1_busa, idu_1_dataa, idu_1_datab, idu_1_imm, S;

  not not_1 (clk_t, clk_out);
  Clock u_clk (.out(clk_out));
  lab5_5_IFU ifu_1 (
    .CLK(clk_t), .Reset(ReSet), .NxtASrc(NxtASrc), .NxtBSrc(NxtBSrc), .Initial_Address(Init_Addr),
    .Imm(idu_1_imm), .BusA(idu_1_busa), .PC(PC), .addr(ifu_1_addr));
  \控制器  \u_控制器_1  (
    .opcode(opcode), .ExtOp(ExtOp), .RegWr(RegWr), .Branch(Branch), .funct3(func3), .ALUASrc(ALUASrc),
    .ALUBSrc(ALUBSrc), .ALUctr(ALUctr), .funct7(func7), .MemtoReg(MemToReg), .MemOp(MemOp), .MemWr(MemWr),
    .Halt(Halt));
  ROM #(.addrWidth(16), .dataWidth(32), .Select("low")) rom_1 (.addr(ifu_1_addr), .data(IR), .sel(ReSet));
  IDU idu_1 (
    .ExtOp(ExtOp), .RegWr(RegWr), .OpCode(opcode), .ALUASrc(ALUASrc), .ALUBSrc(ALUBSrc), .Funct3(func3),
    .Funct7(func7), .BusW(BusW), .PC(PC), .DataA(idu_1_dataa), .BusB(Din), .DataB(idu_1_datab),
    .Imm(idu_1_imm), .BusA(idu_1_busa), .CLK(clk_t), .IR(IR));
  // Probe on Cycles
  Counter #(.width(16), .max('hffff), .behavior("old")) \u_计数器  (
    .count(not_2_out), .Q(Cycles), .clk(clk_t), .clr(ReSet));  // open: load, D, carry, preset
  not not_2 (not_2_out, Halt);
  ALU alu_1 (.A(idu_1_dataa), .B(idu_1_datab), .S(S), .ALUctr(ALUctr), .Zero(alu_1_zero));
  Branch branch_1 (.Branch(Branch), .NxtASrc(NxtASrc), .Zero(alu_1_zero), .NxtBSrc(NxtBSrc), .Result0(S[0]));
  DataRam dataram_1 (
    .Addr(S[17:0]), .Din(Din), .DataOut(dataram_1_dataout), .CLK(clk_t), .CLR(ReSet), .MemOp(MemOp),
    .WE(MemWr));  // open: AlignErr
  Multiplexer #(.width(32), .enable("false")) multiplexer_1 (
    .in0(S), .in1(dataram_1_dataout), .out(BusW), .sel(MemToReg));

  // Notes on the sheet:
  //   输入引脚
  //   请勿修改引脚名称、电路名称及电路封装外观
  //   指令存储器和数据存储器数据位都是32位，指令存储器编址以字为单位，数据存储器编址以字节为单位。
  //   引用取指令部件、取操作数部件、ALU部件、数据存储器、分支控制器、指令存储器等部件，完成单周期CPU设计。
  //   输出引脚
  //   状态元件的触发条件都设置成上升沿触发，时钟输入信号通过反相器输入。
  //   程序执行周期数
endmodule

module Branch (
  input  [2:0] Branch,
  input  Zero,
  input  Result0,
  output NxtASrc,
  output NxtBSrc
);

  wire not_1_out, not_2_out, or_1_out;

  not not_1 (not_1_out, Result0);
  not not_2 (not_2_out, Zero);
  or or_1 (or_1_out, Zero, not_1_out);
  Multiplexer #(.select(3), .enable("false")) multiplexer_1 (
    .in0(1'b0), .in1(1'b1), .in2(1'b1), .in4(Zero), .in5(not_2_out), .in6(Result0), .in7(or_1_out),
    .out(NxtBSrc), .sel(Branch));  // open: in3
  Multiplexer #(.select(3), .enable("false")) multiplexer_2 (
    .in0(1'b0), .in1(1'b0), .in2(1'b1), .in4(1'b0), .in5(1'b0), .in6(1'b0), .in7(1'b0), .out(NxtASrc),
    .sel(Branch));  // open: in3

  // Notes on the sheet:
  //   Zero: pull=down
  //   Branch: pull=down
  //   输入信号
  //   请勿修改引脚名称、电路名称及电路封装外观
  //   不要修改控制信号的编码定义、引脚名称和在布局中的位置。
  //   输出信号
endmodule

module IFU (
  input  [31:0] Initial_Address,
  input  [31:0] Imm,
  input  [31:0] BusA,
  input  CLK,
  input  Reset,
  input  halt,
  input  NxtASrc,
  input  NxtBSrc,
  output [31:0] PC
);

  wire not_1_out;
  wire [31:0] adder_1_out, multiplexer_1_out, multiplexer_2_out, multiplexer_3_out;

  Multiplexer #(.width(32), .enable("false")) multiplexer_1 (
    .in0(PC), .in1(BusA), .out(multiplexer_1_out), .sel(NxtASrc));
  Multiplexer #(.width(32), .enable("false")) multiplexer_2 (
    .in0(32'h4), .in1(Imm), .out(multiplexer_2_out), .sel(NxtBSrc));
  Adder #(.width(32)) adder_1 (.a(multiplexer_1_out), .b(multiplexer_2_out), .out(adder_1_out));  // open: cin, cout
  not not_1 (not_1_out, halt);
  Register #(.width(32), .Select("high")) u_PC (
    .D(multiplexer_3_out), .en(not_1_out), .Q(PC), .clk(CLK), .cs(1'b1));  // open: clr, preset
  Multiplexer #(.width(32), .enable("false")) multiplexer_3 (
    .in0(adder_1_out), .in1(Initial_Address), .out(multiplexer_3_out), .sel(Reset));

  // Other names for the same wires on the sheet: Init_Addr[31:0] = Initial_Address

  // Notes on the sheet:
  //   NxtASrc: pull=down
  //   Imm: pull=down
  //   BusA: pull=down
  //   NxtBSrc: pull=down
  //   输入信号
  //   请勿修改引脚名称、电路名称及电路封装外观
  //   指令存储器256KB，数据位为32位，地址位为16位。PC寄存器数据宽度32位，片选信号高电平有效
  //   输出信号
endmodule

module \控制器  (
  input  [6:0] opcode,
  input  [2:0] funct3,
  input  [6:0] funct7,
  output [2:0] ExtOp,
  output RegWr,
  output [2:0] Branch,
  output ALUASrc,
  output [1:0] ALUBSrc,
  output [3:0] ALUctr,
  output MemtoReg,
  output [2:0] MemOp,
  output MemWr,
  output Halt
);

  wire and_1_out, and_2_out, I_Arith, J_jal, J_jalr, or_1_out, or_8_out, R_Arith, U_auipc, U_lui;

  Comparator #(.width(7)) comparator_1 (.a(opcode), .b(7'b0110111), .eq(U_lui));  // open: gt, lt
  Comparator #(.width(7)) comparator_2 (.a(opcode), .b(7'b1100111), .eq(J_jalr));  // open: gt, lt
  Comparator #(.width(7)) comparator_3 (.a(opcode), .b(7'b0010111), .eq(U_auipc));  // open: gt, lt
  Comparator #(.width(7)) comparator_4 (.a(opcode), .b(7'b1100011), .eq(Branch[2]));  // open: gt, lt
  Comparator #(.width(7)) comparator_5 (.a(opcode), .b(7'b0010011), .eq(I_Arith));  // open: gt, lt
  Comparator #(.width(7)) comparator_6 (.a(opcode), .b(7'b0000011), .eq(MemtoReg));  // open: gt, lt
  or or_1 (or_1_out, U_lui, U_auipc);
  or or_2 (ALUBSrc[0], J_jal, J_jalr);
  and and_1 (and_1_out, Branch[2], funct3[2]);
  and and_2 (and_2_out, Branch[2], funct3[0]);
  Comparator #(.width(7)) comparator_7 (.a(opcode), .b(7'b0110011), .eq(R_Arith));  // open: gt, lt
  Comparator #(.width(7)) comparator_8 (.a(opcode), .b(7'b0100011), .eq(MemWr));  // open: gt, lt
  or or_3 (Branch[1], and_1_out, J_jalr);
  or or_4 (Branch[0], J_jal, and_2_out);
  or or_5 (RegWr, or_1_out, ALUBSrc[0], I_Arith, R_Arith, MemtoReg);
  Comparator #(.width(7)) comparator_9 (.a(opcode), .b(7'b1101111), .eq(J_jal));  // open: gt, lt
  Comparator #(.width(7)) comparator_10 (.a(opcode), .b(7'b1110011), .eq(Halt));  // open: gt, lt
  or or_6 (ALUASrc, U_auipc, ALUBSrc[0]);
  or or_7 (ALUBSrc[1], or_1_out, I_Arith, MemtoReg, MemWr);
  Extop extop_1 (
    .a(opcode[6]), .b(opcode[5]), .c(opcode[4]), .d(opcode[3]), .e(opcode[2]), .f(opcode[1]), .g(opcode[0]),
    .out_8(ExtOp[2]), .out_9(ExtOp[1]), .out_10(ExtOp[0]));
  or or_8 (or_8_out, funct7[5], 1'b0);
  mem2 mem2_1 (
    .in_1(opcode[6]), .in_2(opcode[5]), .in_3(opcode[4]), .in_4(opcode[3]), .in_5(opcode[2]),
    .in_6(opcode[1]), .in_7(opcode[0]), .in_8(funct3[2]), .in_9(funct3[1]), .in_10(funct3[0]),
    .out_11(MemOp[2]));
  mem1 mem1_1 (
    .in_1(opcode[6]), .in_2(opcode[5]), .in_3(opcode[4]), .in_4(opcode[3]), .in_5(opcode[2]),
    .in_6(opcode[1]), .in_7(opcode[0]), .in_8(funct3[2]), .in_9(funct3[1]), .in_10(funct3[0]),
    .out_11(MemOp[1]));
  Aluctr4 aluctr4_1 (
    ._6(opcode[6]), ._5(opcode[5]), ._4(opcode[4]), ._3(opcode[3]), ._2(opcode[2]), ._1(opcode[1]),
    ._0(opcode[0]), .fun32(funct3[2]), .fun31(funct3[1]), .fun30(funct3[0]), .fun75(or_8_out),
    .out_12(ALUctr[3]));
  Aluctr3 aluctr3_1 (
    ._6(opcode[6]), ._5(opcode[5]), ._4(opcode[4]), ._3(opcode[3]), ._2(opcode[2]), ._1(opcode[1]),
    ._0(opcode[0]), .fun2(funct3[2]), .fun1(funct3[1]), .fun0(funct3[0]), .fun75(or_8_out), .out_12(ALUctr[2]));
  Aluctr2 aluctr2_1 (
    ._6(opcode[6]), ._5(opcode[5]), ._4(opcode[4]), ._3(opcode[3]), ._2(opcode[2]), ._1(opcode[1]),
    ._0(opcode[0]), .func32(funct3[2]), .func31(funct3[1]), .fun30(funct3[0]), .in_11(or_8_out),
    .out_12(ALUctr[1]));
  Alutrc1 alutrc1_1 (
    ._6(opcode[6]), ._5(opcode[5]), ._4(opcode[4]), ._3(opcode[3]), ._2(opcode[2]), ._1(opcode[1]),
    ._0(opcode[0]), .fun32(funct3[2]), .fun31(funct3[1]), .fun30(funct3[0]), .fnu75(or_8_out),
    .out_12(ALUctr[0]));
  mem0 mem0_1 (
    .in_1(opcode[6]), .in_2(opcode[5]), .in_3(opcode[4]), .in_4(opcode[3]), .in_5(opcode[2]),
    .in_6(opcode[1]), .in_7(opcode[0]), .in_8(funct3[2]), .in_9(funct3[1]), .in_10(funct3[0]),
    .out_11(MemOp[0]));

  // Other names for the same wires on the sheet: B_Instr = Branch[2]; I_load = MemtoReg; S_Instr = MemWr

  // Notes on the sheet:
  //   输入引脚
  //   请勿修改引脚名称、电路名称及电路封装外观
  //   提示：根据指令种类，把7位指令code用一位指令类型标志位来表示，再通过功能码来区分具体指令，生成控制信号。
  //   输出引脚
endmodule

module RegFile (
  input  [4:0] R1_num,
  input  [4:0] R2_num,
  input  [4:0] Write_Reg_num,
  input  [31:0] Din,
  input  Write_Enable,
  input  Clock,
  output [31:0] Reg1Out,
  output [31:0] Reg2Out
);

  wire and_1_out, and_2_out, and_3_out, and_4_out, and_5_out, and_6_out, and_7_out, and_8_out, and_9_out,
       and_10_out, and_11_out, and_12_out, and_13_out, and_14_out, and_15_out, and_16_out, and_17_out,
       and_18_out, and_19_out, and_20_out, and_21_out, and_22_out, and_23_out, and_24_out, and_25_out,
       and_26_out, and_27_out, and_28_out, and_29_out, and_30_out, and_31_out, and_32_out, decoder_1_out0,
       decoder_1_out1, decoder_1_out2, decoder_1_out3, decoder_1_out4, decoder_1_out5, decoder_1_out6,
       decoder_1_out7, decoder_1_out8, decoder_1_out9, decoder_1_out10, decoder_1_out11, decoder_1_out12,
       decoder_1_out13, decoder_1_out14, decoder_1_out15, decoder_1_out16, decoder_1_out17, decoder_1_out18,
       decoder_1_out19, decoder_1_out20, decoder_1_out21, decoder_1_out22, decoder_1_out23, decoder_1_out24,
       decoder_1_out25, decoder_1_out26, decoder_1_out27, decoder_1_out28, decoder_1_out29, decoder_1_out30,
       decoder_1_out31;
  wire [31:0] _0_q, _1_q, _2_q, _3_q, _4_q, _5_q, _6_q, _7_q, _8_q, _9_q, _10_q, _11_q, _12_q, _13_q, _14_q,
       _15_q, _16_q, _17_q, _18_q, _19_q, _20_q, _21_q, _22_q, _23_q, _24_q, _25_q, _26_q, _27_q, _28_q,
       _29_q, _30_q, _31_q;

  Decoder #(.select(5), .enable("false")) decoder_1 (
    .out0(decoder_1_out0), .out1(decoder_1_out1), .out2(decoder_1_out2), .out3(decoder_1_out3),
    .out4(decoder_1_out4), .out5(decoder_1_out5), .out6(decoder_1_out6), .out7(decoder_1_out7),
    .out8(decoder_1_out8), .out9(decoder_1_out9), .out10(decoder_1_out10), .out11(decoder_1_out11),
    .out12(decoder_1_out12), .out13(decoder_1_out13), .out14(decoder_1_out14), .out15(decoder_1_out15),
    .out16(decoder_1_out16), .out17(decoder_1_out17), .out18(decoder_1_out18), .out19(decoder_1_out19),
    .out20(decoder_1_out20), .out21(decoder_1_out21), .out22(decoder_1_out22), .out23(decoder_1_out23),
    .out24(decoder_1_out24), .out25(decoder_1_out25), .out26(decoder_1_out26), .out27(decoder_1_out27),
    .out28(decoder_1_out28), .out29(decoder_1_out29), .out30(decoder_1_out30), .out31(decoder_1_out31),
    .sel(Write_Reg_num));
  and and_1 (and_1_out, decoder_1_out0, Write_Enable);
  and and_2 (and_2_out, decoder_1_out1, Write_Enable);
  and and_3 (and_3_out, decoder_1_out2, Write_Enable);
  and and_4 (and_4_out, decoder_1_out3, Write_Enable);
  and and_5 (and_5_out, decoder_1_out4, Write_Enable);
  and and_6 (and_6_out, decoder_1_out5, Write_Enable);
  and and_7 (and_7_out, decoder_1_out6, Write_Enable);
  and and_8 (and_8_out, decoder_1_out7, Write_Enable);
  and and_9 (and_9_out, decoder_1_out8, Write_Enable);
  and and_10 (and_10_out, decoder_1_out9, Write_Enable);
  and and_11 (and_11_out, decoder_1_out10, Write_Enable);
  and and_12 (and_12_out, decoder_1_out11, Write_Enable);
  and and_13 (and_13_out, decoder_1_out12, Write_Enable);
  and and_14 (and_14_out, decoder_1_out13, Write_Enable);
  and and_15 (and_15_out, decoder_1_out14, Write_Enable);
  and and_16 (and_16_out, decoder_1_out15, Write_Enable);
  and and_17 (and_17_out, decoder_1_out16, Write_Enable);
  and and_18 (and_18_out, decoder_1_out17, Write_Enable);
  and and_19 (and_19_out, decoder_1_out18, Write_Enable);
  and and_20 (and_20_out, decoder_1_out19, Write_Enable);
  and and_21 (and_21_out, decoder_1_out20, Write_Enable);
  and and_22 (and_22_out, decoder_1_out21, Write_Enable);
  and and_23 (and_23_out, decoder_1_out22, Write_Enable);
  and and_24 (and_24_out, decoder_1_out23, Write_Enable);
  and and_25 (and_25_out, decoder_1_out24, Write_Enable);
  and and_26 (and_26_out, decoder_1_out25, Write_Enable);
  and and_27 (and_27_out, decoder_1_out26, Write_Enable);
  and and_28 (and_28_out, decoder_1_out27, Write_Enable);
  and and_29 (and_29_out, decoder_1_out28, Write_Enable);
  and and_30 (and_30_out, decoder_1_out29, Write_Enable);
  and and_31 (and_31_out, decoder_1_out30, Write_Enable);
  and and_32 (and_32_out, decoder_1_out31, Write_Enable);
  Register #(.width(32), .Select("high")) _0 (.D({32{1'b0}}), .en(and_1_out), .Q(_0_q), .clk(Clock));  // open: clr
  Register #(.width(32), .Select("high")) _1 (.D(Din), .en(and_2_out), .Q(_1_q), .clk(Clock));  // open: clr
  Register #(.width(32), .Select("high")) _2 (.D(Din), .en(and_3_out), .Q(_2_q), .clk(Clock));  // open: clr
  Register #(.width(32), .Select("high")) _3 (.D(Din), .en(and_4_out), .Q(_3_q), .clk(Clock));  // open: clr
  Register #(.width(32), .Select("high")) _4 (.D(Din), .en(and_5_out), .Q(_4_q), .clk(Clock));  // open: clr
  Register #(.width(32), .Select("high")) _5 (.D(Din), .en(and_6_out), .Q(_5_q), .clk(Clock));  // open: clr
  Register #(.width(32), .Select("high")) _6 (.D(Din), .en(and_7_out), .Q(_6_q), .clk(Clock));  // open: clr
  Register #(.width(32), .Select("high")) _7 (.D(Din), .en(and_8_out), .Q(_7_q), .clk(Clock));  // open: clr
  Register #(.width(32), .Select("high")) _8 (.D(Din), .en(and_9_out), .Q(_8_q), .clk(Clock));  // open: clr
  Register #(.width(32), .Select("high")) _9 (.D(Din), .en(and_10_out), .Q(_9_q), .clk(Clock));  // open: clr
  Register #(.width(32), .Select("high")) _10 (.D(Din), .en(and_11_out), .Q(_10_q), .clk(Clock));  // open: clr
  Register #(.width(32), .Select("high")) _11 (.D(Din), .en(and_12_out), .Q(_11_q), .clk(Clock));  // open: clr
  Register #(.width(32), .Select("high")) _12 (.D(Din), .en(and_13_out), .Q(_12_q), .clk(Clock));  // open: clr
  Register #(.width(32), .Select("high")) _13 (.D(Din), .en(and_14_out), .Q(_13_q), .clk(Clock));  // open: clr
  Register #(.width(32), .Select("high")) _14 (.D(Din), .en(and_15_out), .Q(_14_q), .clk(Clock));  // open: clr
  Register #(.width(32), .Select("high")) _15 (.D(Din), .en(and_16_out), .Q(_15_q), .clk(Clock));  // open: clr
  Register #(.width(32), .Select("high")) _16 (.D(Din), .en(and_17_out), .Q(_16_q), .clk(Clock));  // open: clr
  Register #(.width(32), .Select("high")) _17 (.D(Din), .en(and_18_out), .Q(_17_q), .clk(Clock));  // open: clr
  Register #(.width(32), .Select("high")) _18 (.D(Din), .en(and_19_out), .Q(_18_q), .clk(Clock));  // open: clr
  Register #(.width(32), .Select("high")) _19 (.D(Din), .en(and_20_out), .Q(_19_q), .clk(Clock));  // open: clr
  Register #(.width(32), .Select("high")) _20 (.D(Din), .en(and_21_out), .Q(_20_q), .clk(Clock));  // open: clr
  Register #(.width(32), .Select("high")) _21 (.D(Din), .en(and_22_out), .Q(_21_q), .clk(Clock));  // open: clr
  Register #(.width(32), .Select("high")) _22 (.D(Din), .en(and_23_out), .Q(_22_q), .clk(Clock));  // open: clr
  Register #(.width(32), .Select("high")) _23 (.D(Din), .en(and_24_out), .Q(_23_q), .clk(Clock));  // open: clr
  Register #(.width(32), .Select("high")) _24 (.D(Din), .en(and_25_out), .Q(_24_q), .clk(Clock));  // open: clr
  Register #(.width(32), .Select("high")) _25 (.D(Din), .en(and_26_out), .Q(_25_q), .clk(Clock));  // open: clr
  Register #(.width(32), .Select("high")) _26 (.D(Din), .en(and_27_out), .Q(_26_q), .clk(Clock));  // open: clr
  Register #(.width(32), .Select("high")) _27 (.D(Din), .en(and_28_out), .Q(_27_q), .clk(Clock));  // open: clr
  Register #(.width(32), .Select("high")) _28 (.D(Din), .en(and_29_out), .Q(_28_q), .clk(Clock));  // open: clr
  Register #(.width(32), .Select("high")) _29 (.D(Din), .en(and_30_out), .Q(_29_q), .clk(Clock));  // open: clr
  Register #(.width(32), .Select("high")) _30 (.D(Din), .en(and_31_out), .Q(_30_q), .clk(Clock));  // open: clr
  Register #(.width(32), .Select("high")) _31 (.D(Din), .en(and_32_out), .Q(_31_q), .clk(Clock));  // open: clr
  Multiplexer #(.select(5), .width(32), .enable("false")) multiplexer_1 (
    .in0(_0_q), .in1(_1_q), .in2(_2_q), .in3(_3_q), .in4(_4_q), .in5(_5_q), .in6(_6_q), .in7(_7_q),
    .in8(_8_q), .in9(_9_q), .in10(_10_q), .in11(_11_q), .in12(_12_q), .in13(_13_q), .in14(_14_q),
    .in15(_15_q), .in16(_16_q), .in17(_17_q), .in18(_18_q), .in19(_19_q), .in20(_20_q), .in21(_21_q),
    .in22(_22_q), .in23(_23_q), .in24(_24_q), .in25(_25_q), .in26(_26_q), .in27(_27_q), .in28(_28_q),
    .in29(_29_q), .in30(_30_q), .in31(_31_q), .out(Reg1Out), .sel(R1_num));
  Multiplexer #(.select(5), .width(32), .enable("false")) multiplexer_2 (
    .in0(_0_q), .in1(_1_q), .in2(_2_q), .in3(_3_q), .in4(_4_q), .in5(_5_q), .in6(_6_q), .in7(_7_q),
    .in8(_8_q), .in9(_9_q), .in10(_10_q), .in11(_11_q), .in12(_12_q), .in13(_13_q), .in14(_14_q),
    .in15(_15_q), .in16(_16_q), .in17(_17_q), .in18(_18_q), .in19(_19_q), .in20(_20_q), .in21(_21_q),
    .in22(_22_q), .in23(_23_q), .in24(_24_q), .in25(_25_q), .in26(_26_q), .in27(_27_q), .in28(_28_q),
    .in29(_29_q), .in30(_30_q), .in31(_31_q), .out(Reg2Out), .sel(R2_num));

  // Other names for the same wires on the sheet: CLK = Clock; RA[4:0] = R1_num; RB[4:0] = R2_num; RDA[31:0] = Reg1Out;
  //   RDB[31:0] = Reg2Out; RW[4:0] = Write_Reg_num; WE = Write_Enable

  // Notes on the sheet:
  //   输入引脚
  //   请勿修改引脚名称、电路名称及电路封装外观
  //   提示：使用译码器、多路选择器和32位寄存器及逻辑门实现寄存器堆，禁止直接使用存储器组件。
  //   输出引脚
endmodule

module \立即数扩展器  (
  input  [31:0] Instr,
  input  [2:0] Extop,
  output [31:0] imm
);

  wire [11:0] bit_extender_4_out;
  wire [19:0] bit_extender_3_out;
  wire [31:0] bit_extender_1_out, bit_extender_2_out;

  assign bit_extender_1_out = {{20{Instr[31]}}, Instr[31:20]};  // Bit_Extender bit_extender_1
  assign bit_extender_2_out = {{20{Instr[31]}}, {Instr[31:25], Instr[11:7]}};  // Bit_Extender bit_extender_2
  assign bit_extender_3_out = {{19{Instr[31]}}, Instr[31]};  // Bit_Extender bit_extender_3
  assign bit_extender_4_out = {{11{Instr[31]}}, Instr[31]};  // Bit_Extender bit_extender_4
  Multiplexer #(.select(3), .width(32), .enable("false")) multiplexer_1 (
    .in0(bit_extender_1_out), .in1({Instr[31:12], {12{1'b0}}}), .in2(bit_extender_2_out),
    .in3({bit_extender_3_out, Instr[7], Instr[30:25], Instr[11:8], 1'b0}),
    .in4({bit_extender_4_out, Instr[19:12], Instr[20], Instr[30:21], 1'b0}), .out(imm), .sel(Extop));  // open: in5, in6, in7

  // Notes on the sheet:
  //   Extop: pull=down
  //   Instr: pull=down
  //   输入引脚
  //   输出引脚
endmodule
